// Logisim project 16 BIT CPU.circ as structural Verilog
module CPU_MEM_1 (
  input  in_1,
  input  in_2,
  output out_3
);

  wire nand_1_out, nand_2_out, nand_4_out;

  nand nand_1 (nand_1_out, in_1, in_2);
  nand nand_2 (nand_2_out, nand_1_out, in_2);
  nand nand_3 (out_3, nand_1_out, nand_4_out);
  nand nand_4 (nand_4_out, out_3, nand_2_out);

  // Notes on the sheet:
  //   in_2: pull=down
  //   in_1: pull=down
endmodule

module CPU_MEM_8 (
  input  [15:0] in_1,
  input  s,
  output [15:0] out_3
);

  CPU_MEM_1 cpu_mem_1_1 (.in_1(in_1[0]), .in_2(s), .out_3(out_3[0]));
  CPU_MEM_1 cpu_mem_1_2 (.in_1(in_1[1]), .in_2(s), .out_3(out_3[1]));
  CPU_MEM_1 cpu_mem_1_3 (.in_1(in_1[2]), .in_2(s), .out_3(out_3[2]));
  CPU_MEM_1 cpu_mem_1_4 (.in_1(in_1[3]), .in_2(s), .out_3(out_3[3]));
  CPU_MEM_1 cpu_mem_1_5 (.in_1(in_1[4]), .in_2(s), .out_3(out_3[4]));
  CPU_MEM_1 cpu_mem_1_6 (.in_1(in_1[5]), .in_2(s), .out_3(out_3[5]));
  CPU_MEM_1 cpu_mem_1_7 (.in_1(in_1[6]), .in_2(s), .out_3(out_3[6]));
  CPU_MEM_1 cpu_mem_1_8 (.in_1(in_1[7]), .in_2(s), .out_3(out_3[7]));
  CPU_MEM_1 cpu_mem_1_9 (.in_1(in_1[8]), .in_2(s), .out_3(out_3[8]));
  CPU_MEM_1 cpu_mem_1_10 (.in_1(in_1[9]), .in_2(s), .out_3(out_3[9]));
  CPU_MEM_1 cpu_mem_1_11 (.in_1(in_1[10]), .in_2(s), .out_3(out_3[10]));
  CPU_MEM_1 cpu_mem_1_12 (.in_1(in_1[11]), .in_2(s), .out_3(out_3[11]));
  CPU_MEM_1 cpu_mem_1_13 (.in_1(in_1[12]), .in_2(s), .out_3(out_3[12]));
  CPU_MEM_1 cpu_mem_1_14 (.in_1(in_1[13]), .in_2(s), .out_3(out_3[13]));
  CPU_MEM_1 cpu_mem_1_15 (.in_1(in_1[14]), .in_2(s), .out_3(out_3[14]));
  CPU_MEM_1 cpu_mem_1_16 (.in_1(in_1[15]), .in_2(s), .out_3(out_3[15]));

  // Notes on the sheet:
  //   out_3: pull=down
  //   in_1: pull=down
  //   s: pull=down
endmodule

module CPU_ENABLE_8 (
  input  [15:0] in_1,
  input  in_2,
  output [15:0] out_3
);

  wire and_1_out, and_2_out, and_3_out, and_4_out, and_5_out, and_6_out, and_7_out, and_8_out, and_9_out,
       and_10_out, and_11_out, and_12_out, and_13_out, and_14_out, and_15_out, and_16_out;

  assign out_3[0] = in_2 ? and_1_out : 1'bz;  // Controlled_Buffer controlled_buffer_1
  and and_1 (and_1_out, in_1[0], in_2);
  and and_2 (and_2_out, in_1[1], in_2);
  assign out_3[1] = in_2 ? and_2_out : 1'bz;  // Controlled_Buffer controlled_buffer_2
  assign out_3[2] = in_2 ? and_3_out : 1'bz;  // Controlled_Buffer controlled_buffer_3
  and and_3 (and_3_out, in_1[2], in_2);
  assign out_3[3] = in_2 ? and_4_out : 1'bz;  // Controlled_Buffer controlled_buffer_4
  and and_4 (and_4_out, in_1[3], in_2);
  assign out_3[4] = in_2 ? and_5_out : 1'bz;  // Controlled_Buffer controlled_buffer_5
  and and_5 (and_5_out, in_1[4], in_2);
  assign out_3[5] = in_2 ? and_6_out : 1'bz;  // Controlled_Buffer controlled_buffer_6
  and and_6 (and_6_out, in_1[5], in_2);
  assign out_3[6] = in_2 ? and_7_out : 1'bz;  // Controlled_Buffer controlled_buffer_7
  and and_7 (and_7_out, in_1[6], in_2);
  and and_8 (and_8_out, in_1[7], in_2);
  assign out_3[7] = in_2 ? and_8_out : 1'bz;  // Controlled_Buffer controlled_buffer_8
  assign out_3[8] = in_2 ? and_9_out : 1'bz;  // Controlled_Buffer controlled_buffer_9
  and and_9 (and_9_out, in_1[8], in_2);
  assign out_3[9] = in_2 ? and_10_out : 1'bz;  // Controlled_Buffer controlled_buffer_10
  and and_10 (and_10_out, in_1[9], in_2);
  assign out_3[10] = in_2 ? and_11_out : 1'bz;  // Controlled_Buffer controlled_buffer_11
  and and_11 (and_11_out, in_1[10], in_2);
  assign out_3[11] = in_2 ? and_12_out : 1'bz;  // Controlled_Buffer controlled_buffer_12
  and and_12 (and_12_out, in_1[11], in_2);
  assign out_3[12] = in_2 ? and_13_out : 1'bz;  // Controlled_Buffer controlled_buffer_13
  and and_13 (and_13_out, in_1[12], in_2);
  assign out_3[13] = in_2 ? and_14_out : 1'bz;  // Controlled_Buffer controlled_buffer_14
  and and_14 (and_14_out, in_1[13], in_2);
  and and_15 (and_15_out, in_1[14], in_2);
  assign out_3[14] = in_2 ? and_15_out : 1'bz;  // Controlled_Buffer controlled_buffer_15
  assign out_3[15] = in_2 ? and_16_out : 1'bz;  // Controlled_Buffer controlled_buffer_16
  and and_16 (and_16_out, in_1[15], in_2);
endmodule

module CPU_REGISTER_8 (
  input  [15:0] i,
  input  s,
  input  e,
  output [15:0] REG,
  output [15:0] _0
);

  wire [15:0] cpu_enable_8_1_out_3;

  CPU_MEM_8 cpu_mem_8_1 (.s(s), .in_1(i), .out_3(REG));
  CPU_ENABLE_8 cpu_enable_8_1 (.in_2(e), .in_1(REG), .out_3(cpu_enable_8_1_out_3));
  assign _0 = e ? cpu_enable_8_1_out_3 : 16'bz;  // Controlled_Buffer controlled_buffer_1

  // Notes on the sheet:
  //   s: pull=down
  //   i: pull=down
  //   e: pull=down
  //   REG: pull=down
  //   _0: pull=down
endmodule

module CPU_DECODER_4x16 (
  input  [3:0] in_1,
  output L,
  output out_3,
  output out_4,
  output out_5,
  output out_6,
  output out_7,
  output out_8,
  output out_9,
  output out_10,
  output out_11,
  output out_12,
  output out_13,
  output out_14,
  output out_15,
  output out_16,
  output M
);

  wire not_1_out, not_2_out, not_3_out, not_4_out;

  not not_1 (not_1_out, in_1[0]);
  not not_2 (not_2_out, in_1[1]);
  not not_3 (not_3_out, in_1[2]);
  not not_4 (not_4_out, in_1[3]);
  and and_1 (L, not_4_out, not_3_out, not_2_out, not_1_out);
  and and_2 (out_3, not_4_out, not_3_out, not_2_out, in_1[0]);
  and and_3 (out_4, not_4_out, not_3_out, in_1[1], not_1_out);
  and and_4 (out_5, not_4_out, not_3_out, in_1[1], in_1[0]);
  and and_5 (out_6, not_4_out, in_1[2], not_2_out, not_1_out);
  and and_6 (out_7, not_4_out, in_1[2], not_2_out, in_1[0]);
  and and_7 (out_8, not_4_out, in_1[2], in_1[1], not_1_out);
  and and_8 (out_9, not_4_out, in_1[2], in_1[1], in_1[0]);
  and and_9 (out_10, in_1[3], not_3_out, not_2_out, not_1_out);
  and and_10 (out_11, in_1[3], not_3_out, not_2_out, in_1[0]);
  and and_11 (out_12, in_1[3], not_3_out, in_1[1], not_1_out);
  and and_12 (out_13, in_1[3], not_3_out, in_1[1], in_1[0]);
  and and_13 (out_14, in_1[3], in_1[2], not_2_out, not_1_out);
  and and_14 (out_15, in_1[3], in_1[2], not_2_out, in_1[0]);
  and and_15 (out_16, in_1[3], in_1[2], in_1[1], not_1_out);
  and and_16 (M, in_1[3], in_1[2], in_1[1], in_1[0]);

  // Notes on the sheet:
  //   out_4: pull=down
  //   out_3: pull=down
  //   out_11: pull=down
  //   out_6: pull=down
  //   out_10: pull=down
  //   M: pull=down
  //   out_5: pull=down
  //   out_15: pull=down
  //   out_13: pull=down
  //   out_16: pull=down
  //   out_14: pull=down
  //   in_1: pull=down
  //   L: pull=down
  //   out_9: pull=down
  //   out_7: pull=down
  //   out_12: pull=down
  //   out_8: pull=down
endmodule

module CPU_REG_BYTE (
  input  [15:0] i,
  input  RESET,
  input  h,
  input  v,
  input  s,
  input  e,
  output [15:0] o,
  output [15:0] op
);

  wire and_1_out, and_2_out, and_3_out, or_1_out;
  wire [15:0] cpu_register_8_1__0;

  and and_1 (and_1_out, h, v);
  and and_2 (and_2_out, and_1_out, s);
  and and_3 (and_3_out, and_1_out, e);
  or or_1 (or_1_out, RESET, and_2_out);
  CPU_REGISTER_8 cpu_register_8_1 (.i(i), .s(or_1_out), .e(and_3_out), ._0(cpu_register_8_1__0), .REG(op));
  assign o = and_3_out ? cpu_register_8_1__0 : 16'bz;  // Controlled_Buffer controlled_buffer_1

  // Notes on the sheet:
  //   h: pull=down
  //   RESET: pull=down
  //   e: pull=down
  //   s: pull=down
  //   op: pull=down
  //   o: pull=down
  //   v: pull=down
  //   i: pull=down
endmodule

module CPU_RAM_256 (
  input  reset,
  input  [15:0] i,
  input  sa,
  input  [15:0] address,
  input  s,
  input  e,
  output [15:0] o,
  output [15:0] _15,
  output [15:0] _14,
  output [15:0] _16,
  output [15:0] _12,
  output [15:0] _11,
  output [15:0] _10,
  output [15:0] _9,
  output [15:0] _8,
  output [15:0] _7,
  output [15:0] _6,
  output [15:0] _5,
  output [15:0] _4,
  output [15:0] _21,
  output [15:0] _2,
  output [15:0] _1,
  output [15:0] _0,
  output [15:0] _31,
  output [15:0] _30,
  output [15:0] _29,
  output [15:0] _28,
  output [15:0] _27,
  output [15:0] _26,
  output [15:0] _25,
  output [15:0] _24,
  output [15:0] _23,
  output [15:0] _22,
  output [15:0] _21_2,
  output [15:0] _20,
  output [15:0] _19,
  output [15:0] _18,
  output [15:0] _17,
  output [15:0] _16_2,
  output [7:0] _47,
  output [7:0] _46,
  output [7:0] _45,
  output [7:0] _44,
  output [7:0] _43,
  output [7:0] _42,
  output [7:0] _41,
  output [7:0] _40,
  output [7:0] _39,
  output [7:0] _38,
  output [7:0] _37,
  output [7:0] _36,
  output [7:0] _35,
  output [7:0] _34,
  output [7:0] _33,
  output [7:0] _32,
  output [7:0] _63,
  output [7:0] _62,
  output [7:0] _61,
  output [7:0] _60,
  output [7:0] _59,
  output [7:0] _58,
  output [7:0] _57,
  output [7:0] _56,
  output [7:0] _55,
  output [7:0] _54,
  output [7:0] _53,
  output [7:0] _52,
  output [7:0] _51,
  output [7:0] _50,
  output [7:0] _49,
  output [7:0] _48,
  output [7:0] _79,
  output [7:0] _78,
  output [7:0] _77,
  output [7:0] _76,
  output [7:0] _75,
  output [7:0] _74,
  output [7:0] _73,
  output [7:0] _72,
  output [7:0] _71,
  output [7:0] _70,
  output [7:0] _69,
  output [7:0] _68,
  output [7:0] _67,
  output [7:0] _66,
  output [7:0] _65,
  output [7:0] _64,
  output [7:0] _95,
  output [7:0] _94,
  output [7:0] _93,
  output [7:0] _92,
  output [7:0] _91,
  output [7:0] _90,
  output [7:0] _89,
  output [7:0] _88,
  output [7:0] _87,
  output [7:0] _86,
  output [7:0] _85,
  output [7:0] _84,
  output [7:0] _83,
  output [7:0] _82,
  output [7:0] _81,
  output [7:0] _80,
  output [7:0] _111,
  output [7:0] _110,
  output [7:0] _109,
  output [7:0] _108,
  output [7:0] _107,
  output [7:0] _106,
  output [7:0] _105,
  output [7:0] _104,
  output [7:0] _103,
  output [7:0] _102,
  output [7:0] _101,
  output [7:0] _100,
  output [7:0] _99,
  output [7:0] _98,
  output [7:0] _97,
  output [7:0] _96,
  output [7:0] _127,
  output [7:0] _126,
  output [7:0] _125,
  output [7:0] _124,
  output [7:0] _123,
  output [7:0] _122,
  output [7:0] _121,
  output [7:0] _120,
  output [7:0] _119,
  output [7:0] _118,
  output [7:0] _117,
  output [7:0] _116,
  output [7:0] _115,
  output [7:0] _114,
  output [7:0] _113,
  output [7:0] _112,
  output [7:0] _143,
  output [7:0] _142,
  output [7:0] _141,
  output [7:0] _140,
  output [7:0] _139,
  output [7:0] _138,
  output [7:0] _137,
  output [7:0] _136,
  output [7:0] _135,
  output [7:0] _134,
  output [7:0] _133,
  output [7:0] _132,
  output [7:0] _131,
  output [7:0] _130,
  output [7:0] _129,
  output [7:0] _128,
  output [7:0] _159,
  output [7:0] _158,
  output [7:0] _157,
  output [7:0] _156,
  output [7:0] _155,
  output [7:0] _154,
  output [7:0] _153,
  output [7:0] _152,
  output [7:0] _151,
  output [7:0] _150,
  output [7:0] _149,
  output [7:0] _148,
  output [7:0] _147,
  output [7:0] _146,
  output [7:0] _145,
  output [7:0] _144,
  output [7:0] _175,
  output [7:0] _174,
  output [7:0] _173,
  output [7:0] _172,
  output [7:0] _171,
  output [7:0] _170,
  output [7:0] _169,
  output [7:0] _168,
  output [7:0] _167,
  output [7:0] _166,
  output [7:0] _165,
  output [7:0] _164,
  output [7:0] _163,
  output [7:0] _162,
  output [7:0] _161,
  output [7:0] _160,
  output [7:0] _191,
  output [7:0] _190,
  output [7:0] _189,
  output [7:0] _188,
  output [7:0] _187,
  output [7:0] _186,
  output [7:0] _185,
  output [7:0] _184,
  output [7:0] _183,
  output [7:0] _182,
  output [7:0] _181,
  output [7:0] _180,
  output [7:0] _179,
  output [7:0] _178,
  output [7:0] _177,
  output [7:0] _176,
  output [7:0] _207,
  output [7:0] _206,
  output [7:0] _205,
  output [7:0] _204,
  output [7:0] _203,
  output [7:0] _202,
  output [7:0] _201,
  output [7:0] _200,
  output [7:0] _199,
  output [7:0] _198,
  output [7:0] _197,
  output [7:0] _196,
  output [7:0] _195,
  output [7:0] _194,
  output [7:0] _193,
  output [7:0] _192,
  output [7:0] _223,
  output [7:0] _222,
  output [7:0] _221,
  output [7:0] _220,
  output [7:0] _219,
  output [7:0] _218,
  output [7:0] _217,
  output [7:0] _216,
  output [7:0] _215,
  output [7:0] _214,
  output [7:0] _213,
  output [7:0] _212,
  output [7:0] _211,
  output [7:0] _210,
  output [7:0] _209,
  output [7:0] _208,
  output [7:0] _239,
  output [7:0] _238,
  output [7:0] _237,
  output [7:0] _236,
  output [7:0] _235,
  output [7:0] _234,
  output [7:0] _233,
  output [7:0] _232,
  output [7:0] _231,
  output [7:0] _230,
  output [7:0] _229,
  output [7:0] _228,
  output [7:0] _227,
  output [7:0] _226,
  output [7:0] _225,
  output [7:0] _224,
  output [7:0] _255,
  output [7:0] _254,
  output [7:0] _253,
  output [7:0] _252,
  output [7:0] _251,
  output [7:0] _250,
  output [7:0] _249,
  output [7:0] _248,
  output [7:0] _247,
  output [7:0] _246,
  output [7:0] _245,
  output [7:0] _244,
  output [7:0] _243,
  output [7:0] _242,
  output [7:0] _241,
  output [7:0] _240
);

  wire cpu_decoder_4x16_1_l, cpu_decoder_4x16_1_m, cpu_decoder_4x16_1_out_3, cpu_decoder_4x16_1_out_4,
       cpu_decoder_4x16_1_out_5, cpu_decoder_4x16_1_out_6, cpu_decoder_4x16_1_out_7,
       cpu_decoder_4x16_1_out_8, cpu_decoder_4x16_1_out_9, cpu_decoder_4x16_1_out_10,
       cpu_decoder_4x16_1_out_11, cpu_decoder_4x16_1_out_12, cpu_decoder_4x16_1_out_13,
       cpu_decoder_4x16_1_out_14, cpu_decoder_4x16_1_out_15, cpu_decoder_4x16_1_out_16, cpu_decoder_4x16_2_l,
       cpu_decoder_4x16_2_m, cpu_decoder_4x16_2_out_3, cpu_decoder_4x16_2_out_4, cpu_decoder_4x16_2_out_5,
       cpu_decoder_4x16_2_out_6, cpu_decoder_4x16_2_out_7, cpu_decoder_4x16_2_out_8,
       cpu_decoder_4x16_2_out_9, cpu_decoder_4x16_2_out_10, cpu_decoder_4x16_2_out_11,
       cpu_decoder_4x16_2_out_12, cpu_decoder_4x16_2_out_13, cpu_decoder_4x16_2_out_14,
       cpu_decoder_4x16_2_out_15, cpu_decoder_4x16_2_out_16;
  wire [15:0] cpu_mem_8_1_out_3, cpu_reg_byte_1_o;

  CPU_MEM_8 cpu_mem_8_1 (.s(sa), .in_1(address), .out_3(cpu_mem_8_1_out_3));
  CPU_DECODER_4x16 cpu_decoder_4x16_1 (
    .in_1(cpu_mem_8_1_out_3[7:4]), .L(cpu_decoder_4x16_1_l), .out_3(cpu_decoder_4x16_1_out_3),
    .out_4(cpu_decoder_4x16_1_out_4), .out_5(cpu_decoder_4x16_1_out_5), .out_6(cpu_decoder_4x16_1_out_6),
    .out_7(cpu_decoder_4x16_1_out_7), .out_8(cpu_decoder_4x16_1_out_8), .out_9(cpu_decoder_4x16_1_out_9),
    .out_10(cpu_decoder_4x16_1_out_10), .out_11(cpu_decoder_4x16_1_out_11),
    .out_12(cpu_decoder_4x16_1_out_12), .out_13(cpu_decoder_4x16_1_out_13),
    .out_14(cpu_decoder_4x16_1_out_14), .out_15(cpu_decoder_4x16_1_out_15),
    .out_16(cpu_decoder_4x16_1_out_16), .M(cpu_decoder_4x16_1_m));
  assign o = e ? cpu_reg_byte_1_o : 16'bz;  // Controlled_Buffer controlled_buffer_1
  CPU_REG_BYTE cpu_reg_byte_1 (
    .h(cpu_decoder_4x16_1_l), .v(cpu_decoder_4x16_2_m), .i(i), .o(cpu_reg_byte_1_o), .s(s), .e(e),
    .RESET(reset), .op(_15));
  CPU_REG_BYTE cpu_reg_byte_2 (
    .h(cpu_decoder_4x16_1_out_3), .v(cpu_decoder_4x16_2_m), .i(i), .o(cpu_reg_byte_1_o), .s(s), .e(e),
    .RESET(reset), .op(_31));
  CPU_REG_BYTE cpu_reg_byte_3 (
    .h(cpu_decoder_4x16_1_l), .v(cpu_decoder_4x16_2_out_16), .i(i), .o(cpu_reg_byte_1_o), .s(s), .e(e),
    .RESET(reset), .op(_14));
  CPU_REG_BYTE cpu_reg_byte_4 (
    .h(cpu_decoder_4x16_1_out_3), .v(cpu_decoder_4x16_2_out_16), .i(i), .o(cpu_reg_byte_1_o), .s(s), .e(e),
    .RESET(reset), .op(_30));
  CPU_REG_BYTE cpu_reg_byte_5 (
    .h(cpu_decoder_4x16_1_l), .v(cpu_decoder_4x16_2_out_15), .i(i), .o(cpu_reg_byte_1_o), .s(s), .e(e),
    .RESET(reset), .op(_16));
  CPU_REG_BYTE cpu_reg_byte_6 (
    .h(cpu_decoder_4x16_1_out_3), .v(cpu_decoder_4x16_2_out_15), .i(i), .o(cpu_reg_byte_1_o), .s(s), .e(e),
    .RESET(reset), .op(_29));
  CPU_REG_BYTE cpu_reg_byte_7 (
    .h(cpu_decoder_4x16_1_l), .v(cpu_decoder_4x16_2_out_14), .i(i), .o(cpu_reg_byte_1_o), .s(s), .e(e),
    .RESET(reset), .op(_12));
  CPU_REG_BYTE cpu_reg_byte_8 (
    .h(cpu_decoder_4x16_1_out_3), .v(cpu_decoder_4x16_2_out_14), .i(i), .o(cpu_reg_byte_1_o), .s(s), .e(e),
    .RESET(reset), .op(_28));
  CPU_REG_BYTE cpu_reg_byte_9 (
    .h(cpu_decoder_4x16_1_l), .v(cpu_decoder_4x16_2_out_13), .i(i), .o(cpu_reg_byte_1_o), .s(s), .e(e),
    .RESET(reset), .op(_11));
  CPU_REG_BYTE cpu_reg_byte_10 (
    .h(cpu_decoder_4x16_1_out_3), .v(cpu_decoder_4x16_2_out_13), .i(i), .o(cpu_reg_byte_1_o), .s(s), .e(e),
    .RESET(reset), .op(_27));
  CPU_REG_BYTE cpu_reg_byte_11 (
    .h(cpu_decoder_4x16_1_l), .v(cpu_decoder_4x16_2_out_12), .i(i), .o(cpu_reg_byte_1_o), .s(s), .e(e),
    .RESET(reset), .op(_10));
  CPU_REG_BYTE cpu_reg_byte_12 (
    .h(cpu_decoder_4x16_1_out_3), .v(cpu_decoder_4x16_2_out_12), .i(i), .o(cpu_reg_byte_1_o), .s(s), .e(e),
    .RESET(reset), .op(_26));
  CPU_REG_BYTE cpu_reg_byte_13 (
    .h(cpu_decoder_4x16_1_l), .v(cpu_decoder_4x16_2_out_11), .i(i), .o(cpu_reg_byte_1_o), .s(s), .e(e),
    .RESET(reset), .op(_9));
  CPU_REG_BYTE cpu_reg_byte_14 (
    .h(cpu_decoder_4x16_1_out_3), .v(cpu_decoder_4x16_2_out_11), .i(i), .o(cpu_reg_byte_1_o), .s(s), .e(e),
    .RESET(reset), .op(_25));
  CPU_REG_BYTE cpu_reg_byte_15 (
    .h(cpu_decoder_4x16_1_l), .v(cpu_decoder_4x16_2_out_10), .i(i), .o(cpu_reg_byte_1_o), .s(s), .e(e),
    .RESET(reset), .op(_8));
  CPU_REG_BYTE cpu_reg_byte_16 (
    .h(cpu_decoder_4x16_1_out_3), .v(cpu_decoder_4x16_2_out_10), .i(i), .o(cpu_reg_byte_1_o), .s(s), .e(e),
    .RESET(reset), .op(_24));
  CPU_DECODER_4x16 cpu_decoder_4x16_2 (
    .in_1(cpu_mem_8_1_out_3[3:0]), .L(cpu_decoder_4x16_2_l), .out_3(cpu_decoder_4x16_2_out_3),
    .out_4(cpu_decoder_4x16_2_out_4), .out_5(cpu_decoder_4x16_2_out_5), .out_6(cpu_decoder_4x16_2_out_6),
    .out_7(cpu_decoder_4x16_2_out_7), .out_8(cpu_decoder_4x16_2_out_8), .out_9(cpu_decoder_4x16_2_out_9),
    .out_10(cpu_decoder_4x16_2_out_10), .out_11(cpu_decoder_4x16_2_out_11),
    .out_12(cpu_decoder_4x16_2_out_12), .out_13(cpu_decoder_4x16_2_out_13),
    .out_14(cpu_decoder_4x16_2_out_14), .out_15(cpu_decoder_4x16_2_out_15),
    .out_16(cpu_decoder_4x16_2_out_16), .M(cpu_decoder_4x16_2_m));
  CPU_REG_BYTE cpu_reg_byte_17 (
    .h(cpu_decoder_4x16_1_l), .v(cpu_decoder_4x16_2_out_9), .i(i), .o(cpu_reg_byte_1_o), .s(s), .e(e),
    .RESET(reset), .op(_7));
  CPU_REG_BYTE cpu_reg_byte_18 (
    .h(cpu_decoder_4x16_1_out_3), .v(cpu_decoder_4x16_2_out_9), .i(i), .o(cpu_reg_byte_1_o), .s(s), .e(e),
    .RESET(reset), .op(_23));
  CPU_REG_BYTE cpu_reg_byte_19 (
    .h(cpu_decoder_4x16_1_l), .v(cpu_decoder_4x16_2_out_8), .i(i), .o(cpu_reg_byte_1_o), .s(s), .e(e),
    .RESET(reset), .op(_6));
  CPU_REG_BYTE cpu_reg_byte_20 (
    .h(cpu_decoder_4x16_1_out_3), .v(cpu_decoder_4x16_2_out_8), .i(i), .o(cpu_reg_byte_1_o), .s(s), .e(e),
    .RESET(reset), .op(_22));
  CPU_REG_BYTE cpu_reg_byte_21 (
    .h(cpu_decoder_4x16_1_l), .v(cpu_decoder_4x16_2_out_7), .i(i), .o(cpu_reg_byte_1_o), .s(s), .e(e),
    .RESET(reset), .op(_5));
  CPU_REG_BYTE cpu_reg_byte_22 (
    .h(cpu_decoder_4x16_1_out_3), .v(cpu_decoder_4x16_2_out_7), .i(i), .o(cpu_reg_byte_1_o), .s(s), .e(e),
    .RESET(reset), .op(_21_2));
  CPU_REG_BYTE cpu_reg_byte_23 (
    .h(cpu_decoder_4x16_1_l), .v(cpu_decoder_4x16_2_out_6), .i(i), .o(cpu_reg_byte_1_o), .s(s), .e(e),
    .RESET(reset), .op(_4));
  CPU_REG_BYTE cpu_reg_byte_24 (
    .h(cpu_decoder_4x16_1_out_3), .v(cpu_decoder_4x16_2_out_6), .i(i), .o(cpu_reg_byte_1_o), .s(s), .e(e),
    .RESET(reset), .op(_20));
  CPU_REG_BYTE cpu_reg_byte_25 (
    .h(cpu_decoder_4x16_1_l), .v(cpu_decoder_4x16_2_out_5), .i(i), .o(cpu_reg_byte_1_o), .s(s), .e(e),
    .RESET(reset), .op(_21));
  CPU_REG_BYTE cpu_reg_byte_26 (
    .h(cpu_decoder_4x16_1_out_3), .v(cpu_decoder_4x16_2_out_5), .i(i), .o(cpu_reg_byte_1_o), .s(s), .e(e),
    .RESET(reset), .op(_19));
  CPU_REG_BYTE cpu_reg_byte_27 (
    .h(cpu_decoder_4x16_1_l), .v(cpu_decoder_4x16_2_out_4), .i(i), .o(cpu_reg_byte_1_o), .s(s), .e(e),
    .RESET(reset), .op(_2));
  CPU_REG_BYTE cpu_reg_byte_28 (
    .h(cpu_decoder_4x16_1_out_3), .v(cpu_decoder_4x16_2_out_4), .i(i), .o(cpu_reg_byte_1_o), .s(s), .e(e),
    .RESET(reset), .op(_18));
  CPU_REG_BYTE cpu_reg_byte_29 (
    .h(cpu_decoder_4x16_1_l), .v(cpu_decoder_4x16_2_out_3), .i(i), .o(cpu_reg_byte_1_o), .s(s), .e(e),
    .RESET(reset), .op(_1));
  CPU_REG_BYTE cpu_reg_byte_30 (
    .h(cpu_decoder_4x16_1_out_3), .v(cpu_decoder_4x16_2_out_3), .i(i), .o(cpu_reg_byte_1_o), .s(s), .e(e),
    .RESET(reset), .op(_17));
  CPU_REG_BYTE cpu_reg_byte_31 (
    .h(cpu_decoder_4x16_1_l), .v(cpu_decoder_4x16_2_l), .i(i), .o(cpu_reg_byte_1_o), .s(s), .e(e),
    .RESET(reset), .op(_0));
  CPU_REG_BYTE cpu_reg_byte_32 (
    .h(cpu_decoder_4x16_1_out_3), .v(cpu_decoder_4x16_2_l), .i(i), .o(cpu_reg_byte_1_o), .s(s), .e(e),
    .RESET(reset), .op(_16_2));

  // Notes on the sheet:
  //   _7: pull=up
  //   o: pull=down
  //   _0: pull=down
  //   _4: pull=up
  //   _6: pull=up
  //   _2: pull=up
  //   sa: pull=down
  //   reset: pull=down
  //   address: pull=down
  //   i: pull=down
endmodule

module CPU_NOT (
  input  [15:0] i,
  output [15:0] out_2
);

  not not_1 (out_2[0], i[0]);
  not not_2 (out_2[1], i[1]);
  not not_3 (out_2[2], i[2]);
  not not_4 (out_2[3], i[3]);
  not not_5 (out_2[4], i[4]);
  not not_6 (out_2[5], i[5]);
  not not_7 (out_2[6], i[6]);
  not not_8 (out_2[7], i[7]);
  not not_9 (out_2[8], i[8]);
  not not_10 (out_2[9], i[9]);
  not not_11 (out_2[10], i[10]);
  not not_12 (out_2[11], i[11]);
  not not_13 (out_2[12], i[12]);
  not not_14 (out_2[13], i[13]);
  not not_15 (out_2[14], i[14]);
  not not_16 (out_2[15], i[15]);
endmodule

module CPU_AND (
  input  [15:0] a,
  input  [15:0] b,
  output [15:0] o
);

  and and_1 (o[0], a[0], b[0]);
  and and_2 (o[1], a[1], b[1]);
  and and_3 (o[2], a[2], b[2]);
  and and_4 (o[3], a[3], b[3]);
  and and_5 (o[4], a[4], b[4]);
  and and_6 (o[5], a[5], b[5]);
  and and_7 (o[6], a[6], b[6]);
  and and_8 (o[7], a[7], b[7]);
  and and_9 (o[8], a[8], b[8]);
  and and_10 (o[9], a[9], b[9]);
  and and_11 (o[10], a[10], b[10]);
  and and_12 (o[11], a[11], b[11]);
  and and_13 (o[12], a[12], b[12]);
  and and_14 (o[13], a[13], b[13]);
  and and_15 (o[14], a[14], b[14]);
  and and_16 (o[15], a[15], b[15]);
endmodule

module CPU_OR (
  input  [15:0] a,
  input  [15:0] b,
  output [15:0] _0
);

  or or_1 (_0[0], a[0], b[0]);
  or or_2 (_0[1], a[1], b[1]);
  or or_3 (_0[2], a[2], b[2]);
  or or_4 (_0[3], a[3], b[3]);
  or or_5 (_0[4], a[4], b[4]);
  or or_6 (_0[5], a[5], b[5]);
  or or_7 (_0[6], a[6], b[6]);
  or or_8 (_0[7], a[7], b[7]);
  or or_9 (_0[8], a[8], b[8]);
  or or_10 (_0[9], a[9], b[9]);
  or or_11 (_0[10], a[10], b[10]);
  or or_12 (_0[11], a[11], b[11]);
  or or_13 (_0[12], a[12], b[12]);
  or or_14 (_0[13], a[13], b[13]);
  or or_15 (_0[14], a[14], b[14]);
  or or_16 (_0[15], a[15], b[15]);
endmodule

module CPU_XOR_1 (
  input  a,
  input  b,
  output o
);

  wire nand_1_out, nand_2_out, not_1_out, not_2_out;

  not not_1 (not_1_out, a);
  not not_2 (not_2_out, b);
  nand nand_1 (nand_1_out, not_1_out, b);
  nand nand_2 (nand_2_out, a, not_2_out);
  nand nand_3 (o, nand_1_out, nand_2_out);
endmodule

module CPU_SHR (
  input  [15:0] i,
  input  shift_in,
  output shift_out,
  output [15:0] o
);

  wire [15:1] cpu_register_8_1__0;

  CPU_REGISTER_8 cpu_register_8_1 (.i(i), .s(1'b1), .e(1'b1), ._0({cpu_register_8_1__0, shift_out}));  // open: REG
  CPU_REGISTER_8 cpu_register_8_2 (.i({shift_in, cpu_register_8_1__0}), .s(1'b1), .e(1'b1), ._0(o));  // open: REG
endmodule

module CPU_SHL (
  input  shift_in,
  input  [15:0] i,
  output [15:0] o,
  output shift_out
);

  wire [14:0] cpu_register_8_1__0;

  CPU_REGISTER_8 cpu_register_8_1 (.i(i), .s(1'b1), .e(1'b1), ._0({shift_out, cpu_register_8_1__0}));  // open: REG
  CPU_REGISTER_8 cpu_register_8_2 (.i({cpu_register_8_1__0, shift_in}), .s(1'b1), .e(1'b1), ._0(o));  // open: REG
endmodule

module CPU_ADDER (
  input  a,
  input  b,
  input  carry_in,
  output sum,
  output carry_out
);

  wire and_1_out, and_2_out, cpu_xor_1_1_o;

  CPU_XOR_1 cpu_xor_1_1 (.a(a), .b(b), .o(cpu_xor_1_1_o));
  and and_1 (and_1_out, carry_in, cpu_xor_1_1_o);
  and and_2 (and_2_out, a, b);
  CPU_XOR_1 cpu_xor_1_2 (.a(cpu_xor_1_1_o), .b(carry_in), .o(sum));
  or or_1 (carry_out, and_1_out, and_2_out);
endmodule

module CPU_ADDER_8 (
  input  [15:0] a,
  input  [15:0] b,
  input  carry_in,
  output carry_out,
  output [15:0] out_5
);

  wire cpu_adder_2_carry_out, cpu_adder_3_carry_out, cpu_adder_4_carry_out, cpu_adder_5_carry_out,
       cpu_adder_6_carry_out, cpu_adder_7_carry_out, cpu_adder_8_carry_out, cpu_adder_9_carry_out,
       cpu_adder_10_carry_out, cpu_adder_11_carry_out, cpu_adder_12_carry_out, cpu_adder_13_carry_out,
       cpu_adder_14_carry_out, cpu_adder_15_carry_out, cpu_adder_16_carry_out;

  CPU_ADDER cpu_adder_1 (.a(a[0]), .b(b[0]), .carry_in(cpu_adder_2_carry_out), .sum(out_5[0]), .carry_out(carry_out));
  CPU_ADDER cpu_adder_2 (
    .a(a[1]), .b(b[1]), .carry_in(cpu_adder_3_carry_out), .sum(out_5[1]), .carry_out(cpu_adder_2_carry_out));
  CPU_ADDER cpu_adder_3 (
    .a(a[2]), .b(b[2]), .carry_in(cpu_adder_4_carry_out), .sum(out_5[2]), .carry_out(cpu_adder_3_carry_out));
  CPU_ADDER cpu_adder_4 (
    .a(a[3]), .b(b[3]), .carry_in(cpu_adder_5_carry_out), .sum(out_5[3]), .carry_out(cpu_adder_4_carry_out));
  CPU_ADDER cpu_adder_5 (
    .a(a[4]), .b(b[4]), .carry_in(cpu_adder_6_carry_out), .sum(out_5[4]), .carry_out(cpu_adder_5_carry_out));
  CPU_ADDER cpu_adder_6 (
    .a(a[5]), .b(b[5]), .carry_in(cpu_adder_7_carry_out), .sum(out_5[5]), .carry_out(cpu_adder_6_carry_out));
  CPU_ADDER cpu_adder_7 (
    .a(a[6]), .b(b[6]), .carry_in(cpu_adder_8_carry_out), .sum(out_5[6]), .carry_out(cpu_adder_7_carry_out));
  CPU_ADDER cpu_adder_8 (
    .a(a[7]), .b(b[7]), .carry_in(cpu_adder_9_carry_out), .sum(out_5[7]), .carry_out(cpu_adder_8_carry_out));
  CPU_ADDER cpu_adder_9 (
    .a(a[8]), .b(b[8]), .carry_in(cpu_adder_10_carry_out), .sum(out_5[8]), .carry_out(cpu_adder_9_carry_out));
  CPU_ADDER cpu_adder_10 (
    .a(a[9]), .b(b[9]), .carry_in(cpu_adder_11_carry_out), .sum(out_5[9]), .carry_out(cpu_adder_10_carry_out));
  CPU_ADDER cpu_adder_11 (
    .a(a[10]), .b(b[10]), .carry_in(cpu_adder_12_carry_out), .sum(out_5[10]),
    .carry_out(cpu_adder_11_carry_out));
  CPU_ADDER cpu_adder_12 (
    .a(a[11]), .b(b[11]), .carry_in(cpu_adder_13_carry_out), .sum(out_5[11]),
    .carry_out(cpu_adder_12_carry_out));
  CPU_ADDER cpu_adder_13 (
    .a(a[12]), .b(b[12]), .carry_in(cpu_adder_14_carry_out), .sum(out_5[12]),
    .carry_out(cpu_adder_13_carry_out));
  CPU_ADDER cpu_adder_14 (
    .a(a[13]), .b(b[13]), .carry_in(cpu_adder_15_carry_out), .sum(out_5[13]),
    .carry_out(cpu_adder_14_carry_out));
  CPU_ADDER cpu_adder_15 (
    .a(a[14]), .b(b[14]), .carry_in(cpu_adder_16_carry_out), .sum(out_5[14]),
    .carry_out(cpu_adder_15_carry_out));
  CPU_ADDER cpu_adder_16 (
    .a(a[15]), .b(b[15]), .carry_in(carry_in), .sum(out_5[15]), .carry_out(cpu_adder_16_carry_out));
endmodule

module CPU_XOR_LE_1 (
  input  above_equal,
  input  a_larger,
  input  a,
  input  b,
  output c,
  output equal,
  output a_large
);

  wire and_2_out, not_1_out;

  CPU_XOR_1 cpu_xor_1_1 (.a(a), .b(b), .o(c));
  not not_1 (not_1_out, c);
  and and_1 (equal, not_1_out, above_equal);
  and and_2 (and_2_out, above_equal, a, c);
  or or_1 (a_large, and_2_out, a_larger);
endmodule

module CPU_XOR_LE_8 (
  input  [15:0] a,
  input  [15:0] b,
  output [15:0] out_3,
  output equal,
  output larger
);

  wire cpu_xor_le_1_1_a_large, cpu_xor_le_1_1_equal, cpu_xor_le_1_2_a_large, cpu_xor_le_1_2_equal,
       cpu_xor_le_1_3_a_large, cpu_xor_le_1_3_equal, cpu_xor_le_1_4_a_large, cpu_xor_le_1_4_equal,
       cpu_xor_le_1_5_a_large, cpu_xor_le_1_5_equal, cpu_xor_le_1_6_a_large, cpu_xor_le_1_6_equal,
       cpu_xor_le_1_7_a_large, cpu_xor_le_1_7_equal, cpu_xor_le_1_8_a_large, cpu_xor_le_1_8_equal,
       cpu_xor_le_1_9_a_large, cpu_xor_le_1_9_equal, cpu_xor_le_1_10_a_large, cpu_xor_le_1_10_equal,
       cpu_xor_le_1_11_a_large, cpu_xor_le_1_11_equal, cpu_xor_le_1_12_a_large, cpu_xor_le_1_12_equal,
       cpu_xor_le_1_13_a_large, cpu_xor_le_1_13_equal, cpu_xor_le_1_14_a_large, cpu_xor_le_1_14_equal,
       cpu_xor_le_1_15_a_large, cpu_xor_le_1_15_equal;

  CPU_XOR_LE_1 cpu_xor_le_1_1 (
    .a(a[0]), .b(b[0]), .a_larger(1'b0), .c(out_3[0]), .above_equal(1'b1), .equal(cpu_xor_le_1_1_equal),
    .a_large(cpu_xor_le_1_1_a_large));
  CPU_XOR_LE_1 cpu_xor_le_1_2 (
    .a(a[1]), .b(b[1]), .a_larger(cpu_xor_le_1_1_a_large), .c(out_3[1]), .above_equal(cpu_xor_le_1_1_equal),
    .equal(cpu_xor_le_1_2_equal), .a_large(cpu_xor_le_1_2_a_large));
  CPU_XOR_LE_1 cpu_xor_le_1_3 (
    .a(a[2]), .b(b[2]), .a_larger(cpu_xor_le_1_2_a_large), .c(out_3[2]), .above_equal(cpu_xor_le_1_2_equal),
    .equal(cpu_xor_le_1_3_equal), .a_large(cpu_xor_le_1_3_a_large));
  CPU_XOR_LE_1 cpu_xor_le_1_4 (
    .a(a[3]), .b(b[3]), .a_larger(cpu_xor_le_1_3_a_large), .c(out_3[3]), .above_equal(cpu_xor_le_1_3_equal),
    .equal(cpu_xor_le_1_4_equal), .a_large(cpu_xor_le_1_4_a_large));
  CPU_XOR_LE_1 cpu_xor_le_1_5 (
    .a(a[4]), .b(b[4]), .a_larger(cpu_xor_le_1_4_a_large), .c(out_3[4]), .above_equal(cpu_xor_le_1_4_equal),
    .equal(cpu_xor_le_1_5_equal), .a_large(cpu_xor_le_1_5_a_large));
  CPU_XOR_LE_1 cpu_xor_le_1_6 (
    .a(a[5]), .b(b[5]), .a_larger(cpu_xor_le_1_5_a_large), .c(out_3[5]), .above_equal(cpu_xor_le_1_5_equal),
    .equal(cpu_xor_le_1_6_equal), .a_large(cpu_xor_le_1_6_a_large));
  CPU_XOR_LE_1 cpu_xor_le_1_7 (
    .a(a[6]), .b(b[6]), .a_larger(cpu_xor_le_1_6_a_large), .c(out_3[6]), .above_equal(cpu_xor_le_1_6_equal),
    .equal(cpu_xor_le_1_7_equal), .a_large(cpu_xor_le_1_7_a_large));
  CPU_XOR_LE_1 cpu_xor_le_1_8 (
    .a(a[7]), .b(b[7]), .a_larger(cpu_xor_le_1_7_a_large), .c(out_3[7]), .above_equal(cpu_xor_le_1_7_equal),
    .equal(cpu_xor_le_1_8_equal), .a_large(cpu_xor_le_1_8_a_large));
  CPU_XOR_LE_1 cpu_xor_le_1_9 (
    .a(a[8]), .b(b[8]), .a_larger(cpu_xor_le_1_8_a_large), .c(out_3[8]), .above_equal(cpu_xor_le_1_8_equal),
    .equal(cpu_xor_le_1_9_equal), .a_large(cpu_xor_le_1_9_a_large));
  CPU_XOR_LE_1 cpu_xor_le_1_10 (
    .a(a[9]), .b(b[9]), .a_larger(cpu_xor_le_1_9_a_large), .c(out_3[9]), .above_equal(cpu_xor_le_1_9_equal),
    .equal(cpu_xor_le_1_10_equal), .a_large(cpu_xor_le_1_10_a_large));
  CPU_XOR_LE_1 cpu_xor_le_1_11 (
    .a(a[10]), .b(b[10]), .a_larger(cpu_xor_le_1_10_a_large), .c(out_3[10]),
    .above_equal(cpu_xor_le_1_10_equal), .equal(cpu_xor_le_1_11_equal), .a_large(cpu_xor_le_1_11_a_large));
  CPU_XOR_LE_1 cpu_xor_le_1_12 (
    .a(a[11]), .b(b[11]), .a_larger(cpu_xor_le_1_11_a_large), .c(out_3[11]),
    .above_equal(cpu_xor_le_1_11_equal), .equal(cpu_xor_le_1_12_equal), .a_large(cpu_xor_le_1_12_a_large));
  CPU_XOR_LE_1 cpu_xor_le_1_13 (
    .a(a[12]), .b(b[12]), .a_larger(cpu_xor_le_1_12_a_large), .c(out_3[12]),
    .above_equal(cpu_xor_le_1_12_equal), .equal(cpu_xor_le_1_13_equal), .a_large(cpu_xor_le_1_13_a_large));
  CPU_XOR_LE_1 cpu_xor_le_1_14 (
    .a(a[13]), .b(b[13]), .a_larger(cpu_xor_le_1_13_a_large), .c(out_3[13]),
    .above_equal(cpu_xor_le_1_13_equal), .equal(cpu_xor_le_1_14_equal), .a_large(cpu_xor_le_1_14_a_large));
  CPU_XOR_LE_1 cpu_xor_le_1_15 (
    .a(a[14]), .b(b[14]), .a_larger(cpu_xor_le_1_14_a_large), .c(out_3[14]),
    .above_equal(cpu_xor_le_1_14_equal), .equal(cpu_xor_le_1_15_equal), .a_large(cpu_xor_le_1_15_a_large));
  CPU_XOR_LE_1 cpu_xor_le_1_16 (
    .a(a[15]), .b(b[15]), .a_larger(cpu_xor_le_1_15_a_large), .c(out_3[15]),
    .above_equal(cpu_xor_le_1_15_equal), .equal(equal), .a_large(larger));
endmodule

module CPU_Z (
  input  [15:0] i,
  output o
);

  wire or_1_out;

  or or_1 (or_1_out, i[0], i[1], i[2], i[3], i[4], i[5], i[6], i[7], i[8], i[9], i[10], i[11], i[12], i[13], i[14], i[15]);
  not not_1 (o, or_1_out);

  // Notes on the sheet:
  //   i: pull=down
endmodule

module CPU_DECODER_3x8 (
  input  c,
  input  b,
  input  a,
  output [7:0] o
);

  wire not_1_out, not_2_out, not_3_out;

  not not_1 (not_1_out, a);
  not not_2 (not_2_out, b);
  not not_3 (not_3_out, c);
  and and_1 (o[0], not_3_out, not_2_out, not_1_out);
  and and_2 (o[1], not_3_out, not_2_out, a);
  and and_3 (o[2], not_3_out, b, not_1_out);
  and and_4 (o[3], not_3_out, b, a);
  and and_5 (o[4], c, not_2_out, not_1_out);
  and and_6 (o[5], c, not_2_out, a);
  and and_7 (o[6], c, b, not_1_out);
  and and_8 (o[7], c, b, a);

  // Notes on the sheet:
  //   o: pull=down
  //   c: pull=down
  //   a: pull=down
  //   b: pull=down
  //   msb
  //   lsb
endmodule

module CPU_E (
  input  [15:0] in_1,
  input  in_2,
  output [15:0] out_3
);

  wire and_1_out, and_2_out, and_3_out, and_4_out, and_5_out, and_6_out, and_7_out, and_8_out, and_9_out,
       and_10_out, and_11_out, and_12_out, and_13_out, and_14_out, and_15_out, and_16_out;

  and and_1 (and_1_out, in_1[0], in_2);
  assign out_3[0] = in_2 ? and_1_out : 1'bz;  // Controlled_Buffer controlled_buffer_1
  and and_2 (and_2_out, in_1[1], in_2);
  assign out_3[1] = in_2 ? and_2_out : 1'bz;  // Controlled_Buffer controlled_buffer_2
  assign out_3[2] = in_2 ? and_3_out : 1'bz;  // Controlled_Buffer controlled_buffer_3
  and and_3 (and_3_out, in_1[2], in_2);
  assign out_3[3] = in_2 ? and_4_out : 1'bz;  // Controlled_Buffer controlled_buffer_4
  and and_4 (and_4_out, in_1[3], in_2);
  assign out_3[4] = in_2 ? and_5_out : 1'bz;  // Controlled_Buffer controlled_buffer_5
  and and_5 (and_5_out, in_1[4], in_2);
  assign out_3[5] = in_2 ? and_6_out : 1'bz;  // Controlled_Buffer controlled_buffer_6
  and and_6 (and_6_out, in_1[5], in_2);
  assign out_3[6] = in_2 ? and_7_out : 1'bz;  // Controlled_Buffer controlled_buffer_7
  and and_7 (and_7_out, in_1[6], in_2);
  assign out_3[7] = in_2 ? and_8_out : 1'bz;  // Controlled_Buffer controlled_buffer_8
  and and_8 (and_8_out, in_1[7], in_2);
  assign out_3[8] = in_2 ? and_9_out : 1'bz;  // Controlled_Buffer controlled_buffer_9
  and and_9 (and_9_out, in_1[8], in_2);
  assign out_3[9] = in_2 ? and_10_out : 1'bz;  // Controlled_Buffer controlled_buffer_10
  and and_10 (and_10_out, in_1[9], in_2);
  and and_11 (and_11_out, in_1[10], in_2);
  assign out_3[10] = in_2 ? and_11_out : 1'bz;  // Controlled_Buffer controlled_buffer_11
  and and_12 (and_12_out, in_1[11], in_2);
  assign out_3[11] = in_2 ? and_12_out : 1'bz;  // Controlled_Buffer controlled_buffer_12
  and and_13 (and_13_out, in_1[12], in_2);
  assign out_3[12] = in_2 ? and_13_out : 1'bz;  // Controlled_Buffer controlled_buffer_13
  and and_14 (and_14_out, in_1[13], in_2);
  assign out_3[13] = in_2 ? and_14_out : 1'bz;  // Controlled_Buffer controlled_buffer_14
  and and_15 (and_15_out, in_1[14], in_2);
  assign out_3[14] = in_2 ? and_15_out : 1'bz;  // Controlled_Buffer controlled_buffer_15
  and and_16 (and_16_out, in_1[15], in_2);
  assign out_3[15] = in_2 ? and_16_out : 1'bz;  // Controlled_Buffer controlled_buffer_16
endmodule

module CPU_ALU (
  input  [15:0] a,
  input  [15:0] b,
  input  carry_in,
  input  a_2,
  input  b_2,
  input  c,
  output a_larger,
  output equal,
  output zero,
  output [15:0] c_2,
  output carry_out
);

  wire and_1_out, and_2_out, and_3_out, cpu_adder_8_1_carry_out, cpu_shl_1_shift_out, cpu_shr_1_shift_out;
  wire [7:0] cpu_decoder_3x8_1_o;
  wire [15:0] cpu_adder_8_1_out_5, cpu_and_1_o, cpu_not_1_out_2, cpu_or_1__0, cpu_shl_1_o, cpu_shr_1_o,
       cpu_xor_le_8_1_out_3;

  CPU_XOR_LE_8 cpu_xor_le_8_1 (.a(a), .b(b), .out_3(cpu_xor_le_8_1_out_3), .larger(a_larger), .equal(equal));
  CPU_AND cpu_and_1 (.a(a), .o(cpu_and_1_o), .b(b));
  CPU_NOT cpu_not_1 (.i(a), .out_2(cpu_not_1_out_2));
  CPU_SHL cpu_shl_1 (.shift_in(carry_in), .i(a), .o(cpu_shl_1_o), .shift_out(cpu_shl_1_shift_out));
  CPU_SHR cpu_shr_1 (.shift_out(cpu_shr_1_shift_out), .i(a), .o(cpu_shr_1_o), .shift_in(carry_in));
  CPU_ADDER_8 cpu_adder_8_1 (
    .a(a), .b(b), .carry_out(cpu_adder_8_1_carry_out), .out_5(cpu_adder_8_1_out_5), .carry_in(carry_in));
  CPU_OR cpu_or_1 (.a(a), .b(b), ._0(cpu_or_1__0));
  CPU_DECODER_3x8 cpu_decoder_3x8_1 (.b(b_2), .o(cpu_decoder_3x8_1_o), .c(c), .a(a_2));
  CPU_E cpu_e_1 (.in_1(cpu_xor_le_8_1_out_3), .out_3(c_2), .in_2(cpu_decoder_3x8_1_o[6]));
  CPU_E cpu_e_2 (.in_1(cpu_or_1__0), .out_3(c_2), .in_2(cpu_decoder_3x8_1_o[5]));
  CPU_E cpu_e_3 (.in_1(cpu_and_1_o), .out_3(c_2), .in_2(cpu_decoder_3x8_1_o[4]));
  CPU_E cpu_e_4 (.in_1(cpu_not_1_out_2), .out_3(c_2), .in_2(cpu_decoder_3x8_1_o[3]));
  CPU_E cpu_e_5 (.in_1(cpu_shl_1_o), .out_3(c_2), .in_2(cpu_decoder_3x8_1_o[2]));
  CPU_E cpu_e_6 (.in_1(cpu_shr_1_o), .out_3(c_2), .in_2(cpu_decoder_3x8_1_o[1]));
  CPU_E cpu_e_7 (.in_1(cpu_adder_8_1_out_5), .out_3(c_2), .in_2(cpu_decoder_3x8_1_o[0]));
  and and_1 (and_1_out, cpu_shl_1_shift_out, cpu_decoder_3x8_1_o[2]);
  assign carry_out = cpu_decoder_3x8_1_o[2] ? and_1_out : 1'bz;  // Controlled_Buffer controlled_buffer_1
  assign carry_out = cpu_decoder_3x8_1_o[1] ? and_2_out : 1'bz;  // Controlled_Buffer controlled_buffer_2
  and and_2 (and_2_out, cpu_shr_1_shift_out, cpu_decoder_3x8_1_o[1]);
  assign carry_out = cpu_decoder_3x8_1_o[0] ? and_3_out : 1'bz;  // Controlled_Buffer controlled_buffer_3
  and and_3 (and_3_out, cpu_adder_8_1_carry_out, cpu_decoder_3x8_1_o[0]);
  CPU_Z cpu_z_1 (.i(c_2), .o(zero));

  // Notes on the sheet:
  //   a_2: pull=down
  //   carry_in: pull=down
  //   b: pull=down
  //   zero: pull=down
  //   b_2: pull=down
  //   a_larger: pull=down
  //   carry_out: pull=down
  //   c_2: pull=down
  //   a: pull=down
  //   c: pull=down
  //   equal: pull=down
endmodule

module CPU_BUS_1 (
  input  [15:0] i,
  input  bus_1,
  output [15:0] o
);

  wire not_1_out;

  and and_1 (o[15], i[15], not_1_out);
  and and_2 (o[14], i[14], not_1_out);
  and and_3 (o[13], i[13], not_1_out);
  and and_4 (o[12], i[12], not_1_out);
  and and_5 (o[10], i[10], not_1_out);
  and and_6 (o[11], i[11], not_1_out);
  and and_7 (o[9], i[9], not_1_out);
  and and_8 (o[8], i[8], not_1_out);
  and and_9 (o[7], i[7], not_1_out);
  and and_10 (o[6], i[6], not_1_out);
  and and_11 (o[5], i[5], not_1_out);
  and and_12 (o[4], i[4], not_1_out);
  and and_13 (o[2], i[2], not_1_out);
  and and_14 (o[3], i[3], not_1_out);
  and and_15 (o[1], i[1], not_1_out);
  or or_1 (o[0], i[0], bus_1);
  not not_1 (not_1_out, bus_1);

  // Notes on the sheet:
  //   o: pull=down
  //   i: pull=down
  //   bus_1: pull=down
endmodule

module CPU_ACCUMULATOR (
  input  [15:0] i,
  input  s,
  input  e,
  output [15:0] ACC,
  output [15:0] o
);

  CPU_REGISTER_8 cpu_register_8_1 (.i(i), .s(s), .e(e), ._0(o), .REG(ACC));

  // Notes on the sheet:
  //   s: pull=down
  //   e: pull=down
  //   o: pull=down
  //   i: pull=down
endmodule

module CPU_R (
  input  [15:0] i,
  input  s,
  input  e,
  output [15:0] \reg ,
  output [15:0] o
);

  CPU_REGISTER_8 cpu_register_8_1 (.i(i), .s(s), .e(e), ._0(o), .REG(\reg ));

  // Notes on the sheet:
  //   s: pull=down
  //   reg: pull=down
  //   i: pull=down
  //   o: pull=down
  //   e: pull=down
endmodule

module CPU_TMP (
  input  [15:0] i,
  input  s,
  output [15:0] o
);

  wire [15:0] controlled_buffer_1_out;

  assign controlled_buffer_1_out = s ? i : 16'bz;  // Controlled_Buffer controlled_buffer_1
  CPU_MEM_8 cpu_mem_8_1 (.s(s), .in_1(controlled_buffer_1_out), .out_3(o));

  // Notes on the sheet:
  //   s: pull=down
  //   i: pull=down
  //   o: pull=down
endmodule

module CPU_STEPPER (
  input  reset,
  input  clk,
  output step_1,
  output step_2,
  output step_3,
  output step_4,
  output step_5,
  output step_6,
  output step_7
);

  wire cpu_mem_1_1_out_3, cpu_mem_1_2_out_3, cpu_mem_1_3_out_3, cpu_mem_1_4_out_3, cpu_mem_1_5_out_3,
       cpu_mem_1_6_out_3, cpu_mem_1_7_out_3, cpu_mem_1_8_out_3, cpu_mem_1_9_out_3, cpu_mem_1_10_out_3,
       cpu_mem_1_11_out_3, not_1_out, not_2_out, not_3_out, not_4_out, not_5_out, not_6_out, not_7_out,
       not_8_out, or_1_out, or_2_out;

  not not_1 (not_1_out, clk);
  not not_2 (not_2_out, reset);
  or or_1 (or_1_out, reset, clk);
  or or_2 (or_2_out, reset, not_1_out);
  or or_3 (step_1, reset, not_3_out);
  CPU_MEM_1 cpu_mem_1_1 (.in_1(not_2_out), .in_2(or_1_out), .out_3(cpu_mem_1_1_out_3));
  not not_3 (not_3_out, cpu_mem_1_2_out_3);
  CPU_MEM_1 cpu_mem_1_2 (.in_1(cpu_mem_1_1_out_3), .in_2(or_2_out), .out_3(cpu_mem_1_2_out_3));
  and and_1 (step_2, cpu_mem_1_2_out_3, not_4_out);
  not not_4 (not_4_out, cpu_mem_1_4_out_3);
  CPU_MEM_1 cpu_mem_1_3 (.in_1(cpu_mem_1_2_out_3), .in_2(or_1_out), .out_3(cpu_mem_1_3_out_3));
  CPU_MEM_1 cpu_mem_1_4 (.in_1(cpu_mem_1_3_out_3), .in_2(or_2_out), .out_3(cpu_mem_1_4_out_3));
  and and_2 (step_3, cpu_mem_1_4_out_3, not_5_out);
  CPU_MEM_1 cpu_mem_1_5 (.in_1(cpu_mem_1_4_out_3), .in_2(or_1_out), .out_3(cpu_mem_1_5_out_3));
  not not_5 (not_5_out, cpu_mem_1_6_out_3);
  CPU_MEM_1 cpu_mem_1_6 (.in_1(cpu_mem_1_5_out_3), .in_2(or_2_out), .out_3(cpu_mem_1_6_out_3));
  and and_3 (step_4, cpu_mem_1_6_out_3, not_6_out);
  not not_6 (not_6_out, cpu_mem_1_8_out_3);
  CPU_MEM_1 cpu_mem_1_7 (.in_1(cpu_mem_1_6_out_3), .in_2(or_1_out), .out_3(cpu_mem_1_7_out_3));
  and and_4 (step_5, cpu_mem_1_8_out_3, not_7_out);
  CPU_MEM_1 cpu_mem_1_8 (.in_1(cpu_mem_1_7_out_3), .in_2(or_2_out), .out_3(cpu_mem_1_8_out_3));
  CPU_MEM_1 cpu_mem_1_9 (.in_1(cpu_mem_1_8_out_3), .in_2(or_1_out), .out_3(cpu_mem_1_9_out_3));
  not not_7 (not_7_out, cpu_mem_1_10_out_3);
  CPU_MEM_1 cpu_mem_1_10 (.in_1(cpu_mem_1_9_out_3), .in_2(or_2_out), .out_3(cpu_mem_1_10_out_3));
  and and_5 (step_6, cpu_mem_1_10_out_3, not_8_out);
  CPU_MEM_1 cpu_mem_1_11 (.in_1(cpu_mem_1_10_out_3), .in_2(or_1_out), .out_3(cpu_mem_1_11_out_3));
  not not_8 (not_8_out, step_7);
  CPU_MEM_1 cpu_mem_1_12 (.in_1(cpu_mem_1_11_out_3), .in_2(or_2_out), .out_3(step_7));

  // Notes on the sheet:
  //   reset: pull=down
endmodule

module CPU (
  input  clock,
  input  [15:0] RAM_INPUT,
  input  RESET,
  output [15:0] R0,
  output [15:0] R1,
  output [15:0] R2,
  output [15:0] R3,
  output clkl,
  output clke,
  output clks,
  output LOAD,
  output END,
  output S,
  output E,
  output IO,
  output DA,
  output [15:0] out_17,
  output [15:0] out_18,
  output [15:0] out_19,
  output [15:0] BUS_OUTPUT
);

  wire _256, and_1_out, and_2_out, C, cpu_alu_1_a_larger, cpu_alu_1_carry_out, cpu_alu_1_equal,
       cpu_alu_1_zero, cpu_carry_temp_1_o, cpu_control_section_1_acc_e, cpu_control_section_1_acc_s,
       cpu_control_section_1_alu_0, cpu_control_section_1_alu_1, cpu_control_section_1_alu_2,
       cpu_control_section_1_bus_1, cpu_control_section_1_flags_s, cpu_control_section_1_iar_e,
       cpu_control_section_1_iar_s, cpu_control_section_1_ir_s, cpu_control_section_1_mar_s,
       cpu_control_section_1_r0_e, cpu_control_section_1_r0_s, cpu_control_section_1_r1_e,
       cpu_control_section_1_r1_s, cpu_control_section_1_r2_e, cpu_control_section_1_r2_s,
       cpu_control_section_1_r3_e, cpu_control_section_1_r3_s, cpu_control_section_1_ram_e,
       cpu_control_section_1_ram_s, cpu_flags_1_a_2, cpu_flags_1_c_2, cpu_flags_1_e_2, cpu_flags_1_z_2,
       not_1_out, not_2_out, S_t;
  wire [7:0] cpu_ram_256_1__56;
  wire [15:0] cpu_alu_1_c_2, cpu_bus_1_1_o, cpu_tmp_1_o, load_256_count_1_count, multiplexer_1_out, undriven;

  CPU_ACCUMULATOR cpu_accumulator_1 (
    .i(cpu_alu_1_c_2), .o(BUS_OUTPUT), .s(cpu_control_section_1_acc_s), .e(cpu_control_section_1_acc_e),
    .ACC(out_19));
  CPU_TMP cpu_tmp_1 (.i(BUS_OUTPUT), .o(cpu_tmp_1_o), .s(S_t));
  CPU_BUS_1 cpu_bus_1_1 (.i(cpu_tmp_1_o), .bus_1(cpu_control_section_1_bus_1), .o(cpu_bus_1_1_o));
  CPU_ALU cpu_alu_1 (
    .a(BUS_OUTPUT), .b(cpu_bus_1_1_o), .carry_in(and_2_out), .a_2(cpu_control_section_1_alu_0),
    .b_2(cpu_control_section_1_alu_1), .c(cpu_control_section_1_alu_2), .zero(cpu_alu_1_zero),
    .c_2(cpu_alu_1_c_2), .carry_out(cpu_alu_1_carry_out), .a_larger(cpu_alu_1_a_larger),
    .equal(cpu_alu_1_equal));
  not not_1 (not_1_out, END);
  and and_1 (and_1_out, clock, not_1_out);
  and and_2 (and_2_out, cpu_carry_temp_1_o, C);
  CPU_CLK cpu_clk_1 (.clkin(and_1_out), .clks(clks), .clke(clke), .clk(clkl));
  CPU_CARRY_TEMP cpu_carry_temp_1 (.c(cpu_flags_1_c_2), .o(cpu_carry_temp_1_o), .s(S_t));
  assign BUS_OUTPUT = not_2_out ? load_256_count_1_count : 16'bz;  // Controlled_Buffer controlled_buffer_1
  LOAD_256_COUNT load_256_count_1 (
    .count(load_256_count_1_count), .clk(clkl), .carry(_256), .LOAD(not_2_out));  // open: reset
  not not_2 (not_2_out, _256);
  CPU_FLAGS cpu_flags_1 (
    .C(cpu_alu_1_carry_out), .A(cpu_alu_1_a_larger), .E(cpu_alu_1_equal), .Z(cpu_alu_1_zero),
    .C_2(cpu_flags_1_c_2), .A_2(cpu_flags_1_a_2), .E_2(cpu_flags_1_e_2), .Z_2(cpu_flags_1_z_2),
    .s(cpu_control_section_1_flags_s));
  CPU_CONTROL_SECTION cpu_control_section_1 (
    .clks(clks), .clke(clke), .clk(clkl), .MAR_S(cpu_control_section_1_mar_s),
    .ACC_S(cpu_control_section_1_acc_s), .TMP_S(S_t), .FLAGS_S(cpu_control_section_1_flags_s),
    .RAM_S(cpu_control_section_1_ram_s), .IO_CLKS_S(S), .IAR_E(cpu_control_section_1_iar_e),
    .RAM_E(cpu_control_section_1_ram_e), .IO_CLK_E(E), .BUS_1(cpu_control_section_1_bus_1),
    .ACC_E(cpu_control_section_1_acc_e), .IR_S(cpu_control_section_1_ir_s),
    .IAR_S(cpu_control_section_1_iar_s), .R0_S(cpu_control_section_1_r0_s),
    .R1_S(cpu_control_section_1_r1_s), .R2_S(cpu_control_section_1_r2_s), .R3_S(cpu_control_section_1_r3_s),
    .R0_E(cpu_control_section_1_r0_e), .R1_E(cpu_control_section_1_r1_e), .R2_E(cpu_control_section_1_r2_e),
    .R3_E(cpu_control_section_1_r3_e), .IR_IN(out_17), .ALU_0(cpu_control_section_1_alu_0),
    .ALU_1(cpu_control_section_1_alu_1), .ALU_2(cpu_control_section_1_alu_2), .C(cpu_flags_1_c_2),
    .A(cpu_flags_1_a_2), .E(cpu_flags_1_e_2), .Z(cpu_flags_1_z_2), .IO(IO), .DA(DA), .RESET(RESET), .C_2(C),
    .END(END), .LOAD(LOAD), ._256(_256));
  CPU_R cpu_r_1 (
    .i(BUS_OUTPUT), .o(BUS_OUTPUT), .s(cpu_control_section_1_r0_s), .e(cpu_control_section_1_r0_e), .\reg (R0));
  CPU_R cpu_r_2 (
    .i(BUS_OUTPUT), .o(BUS_OUTPUT), .s(cpu_control_section_1_r1_s), .e(cpu_control_section_1_r1_e), .\reg (R1));
  CPU_IAR cpu_iar_1 (
    .i(BUS_OUTPUT), .o(BUS_OUTPUT), .s(cpu_control_section_1_iar_s), .e(cpu_control_section_1_iar_e),
    .IAR(out_18));
  CPU_R cpu_r_3 (
    .i(undriven), .o(BUS_OUTPUT), .s(cpu_control_section_1_r2_s), .e(cpu_control_section_1_r2_e), .\reg (R2));
  CPU_IR cpu_ir_1 (.i(BUS_OUTPUT), .o(out_17), .s(cpu_control_section_1_ir_s));
  CPU_R cpu_r_4 (
    .i(BUS_OUTPUT), .o(BUS_OUTPUT), .s(cpu_control_section_1_r3_s), .e(cpu_control_section_1_r3_e), .\reg (R3));
  Multiplexer #(.width(16)) multiplexer_1 (
    .in0(BUS_OUTPUT), .in1(RAM_INPUT), .out(multiplexer_1_out), .sel(LOAD));  // open: en
  CPU_RAM_256 cpu_ram_256_1 (
    .o(BUS_OUTPUT), .sa(cpu_control_section_1_mar_s), .address(BUS_OUTPUT), .s(cpu_control_section_1_ram_s),
    .e(cpu_control_section_1_ram_e), .i(multiplexer_1_out), .reset(RESET), ._56(cpu_ram_256_1__56),
    ._55(cpu_ram_256_1__56));  // open: _0, _2, _4, _6, _7, _8, _9, _10, _11, _12, _14, _15, _31, _30, _29, _28, _27, _26, _25, _24, _23, _22, _21_2, _20, _19, _18, _17, _16_2, _46, _47, _45, _44, _43, _42, _41, _40, _39, _38, _37, _36, _35, _34, _32, _63, _62, _61, _60, _59, _58, _57, _54, _53, _52, _51, _50, _49, _48, _5, _1, _79, _78, _74, _77, _76, _75, _73, _72, _71, _70, _69, _68, _67, _66, _65, _64, _109, _108, _107, _106, _105, _111, _110, _104, _103, _102, _101, _100, _99, _98, _97, _96, _95, _94, _93, _92, _91, _90, _89, _88, _87, _86, _84, _83, _82, _81, _80, _85, _143, _142, _141, _140, _139, _138, _137, _136, _135, _134, _133, _132, _131, _130, _129, _128, _127, _126, _125, _124, _123, _122, _121, _120, _119, _118, _117, _116, _115, _114, _113, _112, _159, _158, _157, _156, _155, _154, _153, _152, _151, _150, _149, _148, _147, _146, _145, _144, _33, _191, _190, _189, _188, _187, _186, _185, _184, _183, _182, _181, _180, _179, _178, _177, _176, _175, _174, _173, _172, _171, _170, _169, _168, _167, _166, _165, _164, _163, _162, _161, _160, _239, _238, _237, _236, _235, _234, _233, _232, _231, _230, _229, _228, _227, _226, _225, _224, _255, _254, _253, _252, _251, _250, _249, _248, _247, _246, _245, _244, _243, _242, _241, _240, _223, _222, _221, _220, _219, _218, _217, _216, _215, _214, _213, _212, _211, _210, _209, _208, _207, _206, _205, _204, _203, _202, _201, _200, _198, _197, _196, _195, _194, _193, _192, _199, _21, _16

  // Notes on the sheet:
  //   out_19: pull=down
  //   out_18: pull=down
  //   R2: pull=down
  //   RAM_INPUT: pull=down
  //   R3: pull=down
  //   out_17: pull=down
  //   R1: pull=down
  //   BUS_OUTPUT: pull=down
  //   LOAD: pull=down
  //   R0: pull=down
endmodule

module CPU_IAR (
  input  [15:0] i,
  input  s,
  input  e,
  output [15:0] IAR,
  output [15:0] o
);

  CPU_REGISTER_8 cpu_register_8_1 (.i(i), .s(s), .e(e), ._0(o), .REG(IAR));

  // Notes on the sheet:
  //   IAR: pull=down
  //   o: pull=down
  //   i: pull=down
  //   e: pull=down
  //   s: pull=down
endmodule

module CPU_IR (
  input  [15:0] i,
  input  s,
  output [15:0] o
);

  CPU_MEM_8 cpu_mem_8_1 (.s(s), .in_1(i), .out_3(o));

  // Notes on the sheet:
  //   s: pull=down
  //   o: pull=down
  //   i: pull=down
endmodule

module CPU_FLAGS (
  input  C,
  input  A,
  input  E,
  input  Z,
  input  s,
  output C_2,
  output A_2,
  output E_2,
  output Z_2
);

  CPU_MEM_1 cpu_mem_1_1 (.in_1(C), .in_2(s), .out_3(C_2));
  CPU_MEM_1 cpu_mem_1_2 (.in_1(A), .in_2(s), .out_3(A_2));
  CPU_MEM_1 cpu_mem_1_3 (.in_1(E), .in_2(s), .out_3(E_2));
  CPU_MEM_1 cpu_mem_1_4 (.in_1(Z), .in_2(s), .out_3(Z_2));

  // Notes on the sheet:
  //   E: pull=down
  //   C_2: pull=down
  //   C: pull=down
  //   Z: pull=down
  //   A: pull=down
  //   Z_2: pull=down
  //   E_2: pull=down
  //   A_2: pull=down
endmodule

module CPU_CONTROL_SECTION (
  input  clks,
  input  clk,
  input  clke,
  input  _256,
  input  RESET,
  input  C,
  input  A,
  input  E,
  input  Z,
  input  [15:0] IR_IN,
  output BUS_1,
  output IR_S,
  output MAR_S,
  output IAR_E,
  output IAR_S,
  output RAM_E,
  output ACC_S,
  output ACC_E,
  output RAM_S,
  output C_2,
  output TMP_S,
  output IO_CLK_E,
  output FLAGS_S,
  output IO_CLKS_S,
  output R0_S,
  output R0_E,
  output R1_S,
  output R1_E,
  output R2_E,
  output R2_S,
  output R3_E,
  output R3_S,
  output END,
  output IO,
  output DA,
  output LOAD,
  output ALU_0,
  output ALU_1,
  output ALU_2
);

  wire and_5_out, and_6_out, and_7_out, and_8_out, and_9_out, and_10_out, and_11_out, and_12_out, and_17_out,
       and_19_out, and_20_out, and_21_out, and_22_out, and_23_out, and_24_out, and_25_out, and_26_out,
       and_27_out, and_28_out, and_29_out, and_30_out, and_31_out, and_32_out, and_33_out, and_34_out,
       and_35_out, and_36_out, and_37_out, and_38_out, and_39_out, and_40_out, and_41_out, and_43_out,
       and_44_out, and_45_out, and_46_out, and_47_out, and_49_out, and_50_out, and_51_out, and_52_out,
       and_53_out, and_54_out, and_55_out, and_56_out, and_57_out, and_58_out, and_59_out, and_60_out,
       and_62_out, and_63_out, and_64_out, and_65_out, clkt, cpu_decoder_2x4_1__0, cpu_decoder_2x4_1__1,
       cpu_decoder_2x4_1__2, cpu_decoder_2x4_1__3, cpu_decoder_2x4_west_1__0, cpu_decoder_2x4_west_1__1,
       cpu_decoder_2x4_west_1__2, cpu_decoder_2x4_west_1__3, cpu_decoder_2x4_west_2__0,
       cpu_decoder_2x4_west_2__1, cpu_decoder_2x4_west_2__2, cpu_decoder_2x4_west_2__3,
       cpu_decoder_cntrl_3x8_1__0, cpu_decoder_cntrl_3x8_1__1, cpu_decoder_cntrl_3x8_1__2,
       cpu_decoder_cntrl_3x8_1__3, cpu_decoder_cntrl_3x8_1__4, cpu_decoder_cntrl_3x8_1__5,
       cpu_decoder_cntrl_3x8_1__6, cpu_decoder_cntrl_3x8_1__7, cpu_stepper_1_step_1, cpu_stepper_1_step_2,
       cpu_stepper_1_step_3, cpu_stepper_1_step_4, cpu_stepper_1_step_5, cpu_stepper_1_step_6,
       cpu_stepper_1_step_7, L1, not_1_out, not_2_out, not_3_out, not_4_out, not_5_out, not_6_out, not_7_out,
       not_8_out, not_9_out, not_10_out, or_6_out, or_7_out, or_8_out, or_9_out, or_10_out, or_11_out,
       or_12_out, or_13_out, or_14_out, or_15_out, or_16_out, or_17_out, or_18_out;

  and and_1 (IAR_E, clke, or_6_out);
  and and_2 (RAM_E, clke, or_7_out);
  and and_3 (ACC_E, clke, or_8_out);
  and and_4 (IO_CLK_E, clke, and_49_out);
  or or_1 (R0_E, and_5_out, and_9_out);
  or or_2 (R1_E, and_6_out, and_10_out);
  or or_3 (R2_E, and_7_out, and_11_out);
  or or_4 (R3_E, and_8_out, and_12_out);
  not not_1 (not_1_out, clk);
  not not_2 (not_2_out, clks);
  and and_5 (and_5_out, clke, or_9_out, cpu_decoder_2x4_west_1__0);
  and and_6 (and_6_out, clke, or_9_out, cpu_decoder_2x4_west_1__1);
  and and_7 (and_7_out, clke, or_9_out, cpu_decoder_2x4_west_1__2);
  and and_8 (and_8_out, clke, or_9_out, cpu_decoder_2x4_west_1__3);
  and and_9 (and_9_out, clke, or_10_out, cpu_decoder_2x4_west_2__0);
  and and_10 (and_10_out, clke, or_10_out, cpu_decoder_2x4_west_2__1);
  and and_11 (and_11_out, clke, or_10_out, cpu_decoder_2x4_west_2__2);
  and and_12 (and_12_out, clke, or_10_out, cpu_decoder_2x4_west_2__3);
  and and_13 (clkt, not_1_out, clke, not_2_out);
  and and_14 (ALU_0, cpu_stepper_1_step_5, IR_IN[7], IR_IN[4]);
  and and_15 (ALU_1, cpu_stepper_1_step_5, IR_IN[7], IR_IN[5]);
  and and_16 (ALU_2, cpu_stepper_1_step_5, IR_IN[7], IR_IN[6]);
  not not_3 (not_3_out, _256);
  or or_5 (BUS_1, and_19_out, and_40_out, and_39_out, and_36_out);
  or or_6 (or_6_out, and_19_out, and_36_out, and_38_out, and_39_out);
  or or_7 (or_7_out, cpu_stepper_1_step_2, and_52_out, and_46_out, and_45_out, and_43_out);
  or or_8 (or_8_out, cpu_stepper_1_step_3, and_47_out, and_51_out, and_50_out);
  or or_9 (or_9_out, and_33_out, and_44_out, and_37_out, and_41_out);
  or or_10 (or_10_out, and_35_out, and_34_out, C_2);
  and and_17 (and_17_out, clk, not_4_out);
  not not_4 (not_4_out, L1);
  not not_5 (not_5_out, L1);
  and and_18 (L1, not_3_out, LOAD);
  CPU_DECODER_2x4_WEST cpu_decoder_2x4_west_1 (
    .a(IR_IN[0]), .b(IR_IN[1]), ._0(cpu_decoder_2x4_west_1__0), ._1(cpu_decoder_2x4_west_1__1),
    ._2(cpu_decoder_2x4_west_1__2), ._3(cpu_decoder_2x4_west_1__3));
  CPU_DECODER_2x4_WEST cpu_decoder_2x4_west_2 (
    .a(IR_IN[2]), .b(IR_IN[8]), ._0(cpu_decoder_2x4_west_2__0), ._1(cpu_decoder_2x4_west_2__1),
    ._2(cpu_decoder_2x4_west_2__2), ._3(cpu_decoder_2x4_west_2__3));
  CPU_STEPPER cpu_stepper_1 (
    .step_1(cpu_stepper_1_step_1), .step_2(cpu_stepper_1_step_2), .step_3(cpu_stepper_1_step_3),
    .step_4(cpu_stepper_1_step_4), .step_5(cpu_stepper_1_step_5), .step_6(cpu_stepper_1_step_6),
    .step_7(cpu_stepper_1_step_7), .reset(cpu_stepper_1_step_7), .clk(and_17_out));
  and and_19 (and_19_out, not_5_out, cpu_stepper_1_step_1);
  not not_6 (not_6_out, IR_IN[7]);
  CPU_DECODER_CNTRL_3x8 cpu_decoder_cntrl_3x8_1 (
    .a(IR_IN[6]), .b(IR_IN[5]), .c(IR_IN[4]), ._0(cpu_decoder_cntrl_3x8_1__0),
    ._1(cpu_decoder_cntrl_3x8_1__1), ._2(cpu_decoder_cntrl_3x8_1__2), ._3(cpu_decoder_cntrl_3x8_1__3),
    ._4(cpu_decoder_cntrl_3x8_1__4), ._5(cpu_decoder_cntrl_3x8_1__5), ._6(cpu_decoder_cntrl_3x8_1__6),
    ._7(cpu_decoder_cntrl_3x8_1__7));
  and and_20 (and_20_out, not_6_out, cpu_decoder_cntrl_3x8_1__0);
  and and_21 (and_21_out, not_6_out, cpu_decoder_cntrl_3x8_1__1);
  and and_22 (and_22_out, not_6_out, cpu_decoder_cntrl_3x8_1__2);
  and and_23 (and_23_out, not_6_out, cpu_decoder_cntrl_3x8_1__3);
  and and_24 (and_24_out, not_6_out, cpu_decoder_cntrl_3x8_1__4);
  and and_25 (and_25_out, not_6_out, cpu_decoder_cntrl_3x8_1__5);
  and and_26 (and_26_out, not_6_out, cpu_decoder_cntrl_3x8_1__6);
  and and_27 (and_27_out, not_6_out, cpu_decoder_cntrl_3x8_1__7);
  not not_7 (not_7_out, IR_IN[5]);
  not not_8 (not_8_out, IR_IN[4]);
  and and_28 (and_28_out, C, IR_IN[3]);
  and and_29 (and_29_out, A, IR_IN[2]);
  and and_30 (and_30_out, E, IR_IN[1]);
  and and_31 (and_31_out, Z, IR_IN[0]);
  or or_11 (or_11_out, and_28_out, and_29_out, and_30_out, and_31_out);
  and and_32 (and_32_out, IR_IN[4], IR_IN[5], IR_IN[6]);
  not not_9 (not_9_out, and_32_out);
  and and_33 (and_33_out, cpu_stepper_1_step_4, IR_IN[7]);
  and and_34 (and_34_out, cpu_stepper_1_step_4, and_20_out);
  and and_35 (and_35_out, cpu_stepper_1_step_4, and_21_out);
  and and_36 (and_36_out, cpu_stepper_1_step_4, and_22_out);
  and and_37 (and_37_out, cpu_stepper_1_step_4, and_23_out);
  and and_38 (and_38_out, cpu_stepper_1_step_4, and_24_out);
  and and_39 (and_39_out, cpu_stepper_1_step_4, and_25_out);
  and and_40 (and_40_out, cpu_stepper_1_step_4, and_26_out);
  and and_41 (and_41_out, cpu_stepper_1_step_4, and_27_out, IR_IN[3]);
  or or_12 (or_12_out, IR_IN[0], IR_IN[1], IR_IN[2], IR_IN[3], IR_IN[4], IR_IN[5], IR_IN[6], IR_IN[7], IR_IN[8], IR_IN[9], IR_IN[10], IR_IN[11], IR_IN[12], IR_IN[13], IR_IN[14], IR_IN[15]);
  and and_42 (C_2, cpu_stepper_1_step_5, IR_IN[7]);
  and and_43 (and_43_out, cpu_stepper_1_step_5, and_20_out);
  and and_44 (and_44_out, cpu_stepper_1_step_5, and_21_out);
  and and_45 (and_45_out, cpu_stepper_1_step_5, and_22_out);
  and and_46 (and_46_out, cpu_stepper_1_step_5, and_24_out);
  and and_47 (and_47_out, cpu_stepper_1_step_5, and_25_out);
  not not_10 (not_10_out, IR_IN[3]);
  and and_48 (END, IR_IN[7], IR_IN[6], not_7_out, not_8_out, IR_IN[3], IR_IN[2], IR_IN[1], IR_IN[0], IR_IN[8], IR_IN[9], IR_IN[10], IR_IN[11], IR_IN[12], IR_IN[13], IR_IN[14], IR_IN[15]);
  not not_11 (LOAD, or_12_out);
  and and_49 (and_49_out, cpu_stepper_1_step_5, and_27_out, not_10_out);
  and and_50 (and_50_out, cpu_stepper_1_step_6, IR_IN[7], not_9_out);
  and and_51 (and_51_out, cpu_stepper_1_step_6, and_22_out);
  and and_52 (and_52_out, cpu_stepper_1_step_6, and_25_out, or_11_out);
  CPU_DECODER_2x4 cpu_decoder_2x4_1 (
    .a(IR_IN[0]), .b(IR_IN[1]), ._0(cpu_decoder_2x4_1__0), ._1(cpu_decoder_2x4_1__1),
    ._2(cpu_decoder_2x4_1__2), ._3(cpu_decoder_2x4_1__3));
  or or_13 (or_13_out, and_19_out, and_36_out, and_39_out, and_34_out, and_35_out, and_38_out);
  or or_14 (or_14_out, cpu_stepper_1_step_3, and_37_out, and_47_out, and_46_out, and_51_out, and_52_out);
  or or_15 (or_15_out, and_19_out, and_36_out, and_39_out, C_2);
  or or_16 (or_16_out, and_40_out, C_2);
  or or_17 (or_17_out, and_43_out, and_50_out, and_45_out, and_49_out);
  and and_53 (and_53_out, clks, cpu_stepper_1_step_2);
  or or_18 (or_18_out, L1, RESET);
  and and_54 (and_54_out, clks, or_13_out);
  and and_55 (and_55_out, clks, or_14_out);
  and and_56 (and_56_out, clks, or_15_out);
  and and_57 (and_57_out, L1, clks);
  and and_58 (and_58_out, clks, and_44_out);
  and and_59 (and_59_out, clks, and_33_out);
  and and_60 (and_60_out, clks, or_16_out);
  and and_61 (IO_CLKS_S, clks, and_41_out);
  and and_62 (and_62_out, clks, or_17_out, cpu_decoder_2x4_1__0);
  and and_63 (and_63_out, clks, or_17_out, cpu_decoder_2x4_1__1);
  and and_64 (and_64_out, clks, or_17_out, cpu_decoder_2x4_1__2);
  and and_65 (and_65_out, clks, or_17_out, cpu_decoder_2x4_1__3);
  or or_19 (IR_S, RESET, and_53_out);
  or or_20 (MAR_S, or_18_out, and_54_out);
  or or_21 (IAR_S, RESET, and_55_out);
  or or_22 (ACC_S, RESET, and_56_out);
  or or_23 (RAM_S, and_57_out, RESET, and_58_out);
  or or_24 (TMP_S, RESET, and_59_out);
  or or_25 (FLAGS_S, RESET, and_60_out);
  or or_26 (R0_S, RESET, and_62_out);
  or or_27 (R1_S, RESET, and_63_out);
  or or_28 (R2_S, RESET, and_64_out);
  or or_29 (R3_S, RESET, and_65_out);

  assign DA = IR_IN[8];
  assign IO = IR_IN[2];

  // Notes on the sheet:
  //   IR_IN: pull=down
  //   _256: pull=down
  //   LOAD: pull=down
  //   END: pull=down
  //   REG B_E
  //   REG A
  //   REG B
  //   REG A
  //   REG B_S
endmodule

module CPU_CLK (
  input  clkin,
  output clk,
  output clks,
  output clke
);

  wire j_k_ff_1_qn, nand_1_out;

  J_K_Flip_Flop j_k_ff_1 (.J(1'b1), .clk(clkin), .K(1'b1), .Q(clk), .Qn(j_k_ff_1_qn));  // open: preset, en, reset
  nand nand_1 (nand_1_out, clkin, clk);
  nand nand_2 (clke, j_k_ff_1_qn, clkin);
  not not_1 (clks, nand_1_out);

  // Notes on the sheet:
  //   clke: pull=down
  //   clkin: pull=down
  //   clk: pull=down
  //   clks: pull=down
endmodule

module CPU_DECODER_2x4 (
  input  a,
  input  b,
  output _0,
  output _1,
  output _2,
  output _3
);

  wire not_1_out, not_2_out;

  not not_1 (not_1_out, b);
  not not_2 (not_2_out, a);
  and and_1 (_0, not_2_out, not_1_out);
  and and_2 (_1, a, not_1_out);
  and and_3 (_2, b, not_2_out);
  and and_4 (_3, b, a);

  // Notes on the sheet:
  //   a: pull=down
  //   b: pull=down
endmodule

module CPU_DECODER_2x4_WEST (
  input  a,
  input  b,
  output _0,
  output _1,
  output _2,
  output _3
);

  wire not_1_out, not_2_out;

  not not_1 (not_1_out, b);
  not not_2 (not_2_out, a);
  and and_1 (_0, not_2_out, not_1_out);
  and and_2 (_1, a, not_1_out);
  and and_3 (_2, b, not_2_out);
  and and_4 (_3, b, a);

  // Notes on the sheet:
  //   a: pull=down
  //   b: pull=down
endmodule

module CPU_DECODER_CNTRL_3x8 (
  input  a,
  input  b,
  input  c,
  output _0,
  output _1,
  output _2,
  output _3,
  output _4,
  output _5,
  output _6,
  output _7
);

  wire not_1_out, not_2_out, not_3_out;

  not not_1 (not_1_out, c);
  not not_2 (not_2_out, b);
  not not_3 (not_3_out, a);
  and and_1 (_0, not_3_out, not_2_out, not_1_out);
  and and_2 (_1, not_3_out, not_2_out, c);
  and and_3 (_2, not_3_out, b, not_1_out);
  and and_4 (_3, not_3_out, b, c);
  and and_5 (_4, a, not_2_out, not_1_out);
  and and_6 (_5, a, not_2_out, c);
  and and_7 (_6, a, b, not_1_out);
  and and_8 (_7, a, b, c);

  // Notes on the sheet:
  //   a: pull=down
  //   b: pull=down
  //   c: pull=down
endmodule

module CPU_TEST (
);

  wire CLK, CLKE, CLKL, CLKS, END, LOAD, load_256_count_1_carry, not_1_out, RESET;
  wire [15:0] ACC, BUS, IAR, IR, load_256_count_1_count, R0, R1, R2, R3, RAM_INPUT;

  Hex_Digit_Display hex_digit_display_1 (.value(BUS[15:12]));  // open: dp
  Hex_Digit_Display hex_digit_display_2 (.value(BUS[11:8]));  // open: dp
  Hex_Digit_Display hex_digit_display_3 (.value(BUS[7:4]));  // open: dp
  CPU cpu_1 (
    .RAM_INPUT(RAM_INPUT), .RESET(RESET), .BUS_OUTPUT(BUS), .R0(R0), .R1(R1), .R2(R2), .R3(R3), .out_17(IR),
    .out_18(IAR), .clock(CLK), .clkl(CLKL), .out_19(ACC), .clks(CLKS), .clke(CLKE), .LOAD(LOAD), .END(END));  // open: S, E, IO, DA
  Hex_Digit_Display hex_digit_display_4 (.value(BUS[3:0]));  // open: dp
  Hex_Digit_Display hex_digit_display_5 (.value(ACC[11:8]));  // open: dp
  Hex_Digit_Display hex_digit_display_6 (.value(ACC[15:12]));  // open: dp
  Hex_Digit_Display hex_digit_display_7 (.value(ACC[7:4]));  // open: dp
  Hex_Digit_Display hex_digit_display_8 (.value(ACC[3:0]));  // open: dp
  Hex_Digit_Display hex_digit_display_9 (.value(IAR[15:12]));  // open: dp
  Hex_Digit_Display hex_digit_display_10 (.value(IAR[11:8]));  // open: dp
  Hex_Digit_Display hex_digit_display_11 (.value(IAR[7:4]));  // open: dp
  Hex_Digit_Display hex_digit_display_12 (.value(IAR[3:0]));  // open: dp
  not not_1 (not_1_out, load_256_count_1_carry);
  Hex_Digit_Display hex_digit_display_13 (.value(IR[11:8]));  // open: dp
  Hex_Digit_Display hex_digit_display_14 (.value(IR[15:12]));  // open: dp
  Button u_RESET (.out(RESET));
  LED #(.active("false")) led_1 (.in(END));
  Hex_Digit_Display hex_digit_display_15 (.value(IR[7:4]));  // open: dp
  Hex_Digit_Display hex_digit_display_16 (.value(IR[3:0]));  // open: dp
  LOAD_256_COUNT load_256_count_1 (
    .count(load_256_count_1_count), .clk(CLKL), .carry(load_256_count_1_carry), .LOAD(not_1_out));  // open: reset
  Hex_Digit_Display hex_digit_display_17 (.value(R0[11:8]));  // open: dp
  Hex_Digit_Display hex_digit_display_18 (.value(R0[15:12]));  // open: dp
  RAM #(.addrWidth(16), .dataWidth(16)) ram_1 (
    .addr(load_256_count_1_count), .data(RAM_INPUT), .sel(not_1_out), .clk(CLKL), .ld(1'b1), .clr(1'b0));
  Clock u_CLK (.out(CLK));
  Hex_Digit_Display hex_digit_display_19 (.value(R0[3:0]));  // open: dp
  Hex_Digit_Display hex_digit_display_20 (.value(R0[7:4]));  // open: dp
  Hex_Digit_Display hex_digit_display_21 (.value(R1[15:12]));  // open: dp
  Hex_Digit_Display hex_digit_display_22 (.value(R1[11:8]));  // open: dp
  Hex_Digit_Display hex_digit_display_23 (.value(R1[7:4]));  // open: dp
  Hex_Digit_Display hex_digit_display_24 (.value(R1[3:0]));  // open: dp
  Hex_Digit_Display hex_digit_display_25 (.value(R2[11:8]));  // open: dp
  Hex_Digit_Display hex_digit_display_26 (.value(R2[15:12]));  // open: dp
  Hex_Digit_Display hex_digit_display_27 (.value(R2[7:4]));  // open: dp
  Hex_Digit_Display hex_digit_display_28 (.value(R2[3:0]));  // open: dp
  Hex_Digit_Display hex_digit_display_29 (.value(R3[15:12]));  // open: dp
  Hex_Digit_Display hex_digit_display_30 (.value(R3[7:4]));  // open: dp
  Hex_Digit_Display hex_digit_display_31 (.value(R3[11:8]));  // open: dp
  Hex_Digit_Display hex_digit_display_32 (.value(R3[3:0]));  // open: dp

  // Notes on the sheet:
  //   BUS
  //   ACC
  //   IAR
  //   IR
  //   EXTERNAL RAM
  //   0
  //   1
  //   0
  //   RO
  //   R1
  //   R2
  //   R3
endmodule

module CPU_CARRY_TEMP (
  input  c,
  input  s,
  output o
);

  CPU_MEM_1 cpu_mem_1_1 (.in_1(c), .in_2(s), .out_3(o));
endmodule

module LOAD_256_COUNT (
  input  clk,
  input  LOAD,
  input  reset,
  output [15:0] count,
  output carry
);

  wire and_1_out;
  wire [15:0] undriven;

  Counter #(.width(16), .max('hffff), .trigger("falling")) counter_1 (
    .D(undriven), .count(1'b1), .Q(count), .carry(carry), .clk(and_1_out), .clr(reset));  // open: load
  and and_1 (and_1_out, LOAD, clk);
endmodule

module CPU_DELAY (
  input  [7:0] i,
  input  clk,
  output [7:0] o
);

  Counter #(.ongoal("stay"), .trigger("falling")) counter_1 (
    .load(1'b1), .D(i), .count(1'b0), .Q(o), .clk(clk));  // open: carry, clr
endmodule

module CPU_TOP_TEMP (
  input  clock
);

  wire and_1_out, C, cpu_alu_1_a_larger, cpu_alu_1_carry_out, cpu_alu_1_equal, cpu_alu_1_zero,
       cpu_carry_temp_1_o, cpu_clk_1_clk, cpu_clk_1_clke, cpu_clk_1_clks, cpu_control_section_1_acc_e,
       cpu_control_section_1_acc_s, cpu_control_section_1_alu_0, cpu_control_section_1_alu_1,
       cpu_control_section_1_alu_2, cpu_control_section_1_bus_1, cpu_control_section_1_flags_s,
       cpu_control_section_1_iar_e, cpu_control_section_1_iar_s, cpu_control_section_1_ir_s,
       cpu_control_section_1_mar_s, cpu_control_section_1_r0_e, cpu_control_section_1_r0_s,
       cpu_control_section_1_r1_e, cpu_control_section_1_r1_s, cpu_control_section_1_r2_e,
       cpu_control_section_1_r2_s, cpu_control_section_1_r3_e, cpu_control_section_1_r3_s,
       cpu_control_section_1_ram_e, cpu_control_section_1_ram_s, cpu_flags_1_a_2, cpu_flags_1_c_2,
       cpu_flags_1_e_2, cpu_flags_1_z_2, cpu_ram_256_1_p7, TMP;
  wire [7:0] cpu_accumulator_1_o_2;
  wire [15:0] cpu_alu_1_c_2, cpu_bus_1_1_o, cpu_ir_1_o, cpu_tmp_1_o;
  wire [15:8] cpu_accumulator_1_o, undriven, undriven_2, undriven_3;

  CPU_TMP cpu_tmp_1 (.i({undriven_2, cpu_accumulator_1_o_2}), .o(cpu_tmp_1_o), .s(TMP));
  CPU_ACCUMULATOR cpu_accumulator_1 (
    .i(cpu_alu_1_c_2), .o({cpu_accumulator_1_o, cpu_accumulator_1_o_2}), .s(cpu_control_section_1_acc_s),
    .e(cpu_control_section_1_acc_e));  // open: ACC
  CPU_BUS_1 cpu_bus_1_1 (.i(cpu_tmp_1_o), .bus_1(cpu_control_section_1_bus_1), .o(cpu_bus_1_1_o));
  and and_1 (and_1_out, cpu_carry_temp_1_o, C);
  CPU_ALU cpu_alu_1 (
    .a({undriven, cpu_accumulator_1_o_2}), .b(cpu_bus_1_1_o), .carry_in(and_1_out),
    .a_2(cpu_control_section_1_alu_0), .b_2(cpu_control_section_1_alu_1), .c(cpu_control_section_1_alu_2),
    .zero(cpu_alu_1_zero), .c_2(cpu_alu_1_c_2), .carry_out(cpu_alu_1_carry_out),
    .a_larger(cpu_alu_1_a_larger), .equal(cpu_alu_1_equal));
  CPU_CLK cpu_clk_1 (.clkin(clock), .clks(cpu_clk_1_clks), .clke(cpu_clk_1_clke), .clk(cpu_clk_1_clk));
  CPU_CARRY_TEMP cpu_carry_temp_1 (.c(cpu_flags_1_c_2), .o(cpu_carry_temp_1_o), .s(TMP));
  CPU_FLAGS cpu_flags_1 (
    .C(cpu_alu_1_carry_out), .A(cpu_alu_1_a_larger), .E(cpu_alu_1_equal), .Z(cpu_alu_1_zero),
    .C_2(cpu_flags_1_c_2), .A_2(cpu_flags_1_a_2), .E_2(cpu_flags_1_e_2), .Z_2(cpu_flags_1_z_2),
    .s(cpu_control_section_1_flags_s));
  CPU_CONTROL_SECTION cpu_control_section_1 (
    .clks(cpu_clk_1_clks), .clke(cpu_clk_1_clke), .clk(cpu_clk_1_clk), .MAR_S(cpu_control_section_1_mar_s),
    .ACC_S(cpu_control_section_1_acc_s), .TMP_S(TMP), .FLAGS_S(cpu_control_section_1_flags_s),
    .RAM_S(cpu_control_section_1_ram_s), .IAR_E(cpu_control_section_1_iar_e),
    .RAM_E(cpu_control_section_1_ram_e), .BUS_1(cpu_control_section_1_bus_1),
    .ACC_E(cpu_control_section_1_acc_e), .IR_S(cpu_control_section_1_ir_s),
    .IAR_S(cpu_control_section_1_iar_s), .R0_S(cpu_control_section_1_r0_s),
    .R1_S(cpu_control_section_1_r1_s), .R2_S(cpu_control_section_1_r2_s), .R3_S(cpu_control_section_1_r3_s),
    .R0_E(cpu_control_section_1_r0_e), .R1_E(cpu_control_section_1_r1_e), .R2_E(cpu_control_section_1_r2_e),
    .R3_E(cpu_control_section_1_r3_e), .IR_IN(cpu_ir_1_o), .ALU_0(cpu_control_section_1_alu_0),
    .ALU_1(cpu_control_section_1_alu_1), .ALU_2(cpu_control_section_1_alu_2), .C(cpu_flags_1_c_2),
    .A(cpu_flags_1_a_2), .E(cpu_flags_1_e_2), .Z(cpu_flags_1_z_2), .C_2(C));  // open: IO_CLKS_S, IO_CLK_E, IO, DA, RESET, END, LOAD, _256
  // CPU_R cpu_r_1: pin names not known; wires that end beside it: cpu_accumulator_1_o_2, cpu_control_section_1_r0_s, cpu_accumulator_1_o_2, cpu_control_section_1_r0_e
  // CPU_R cpu_r_2: pin names not known; wires that end beside it: cpu_accumulator_1_o_2, cpu_control_section_1_r1_s, cpu_accumulator_1_o_2, cpu_control_section_1_r1_e
  // CPU_IAR cpu_iar_1: pin names not known; wires that end beside it: cpu_control_section_1_iar_s, cpu_accumulator_1_o_2, cpu_control_section_1_iar_e, cpu_accumulator_1_o_2
  // CPU_R cpu_r_3: pin names not known; wires that end beside it: cpu_accumulator_1_o_2, cpu_control_section_1_r2_s, cpu_accumulator_1_o_2, cpu_control_section_1_r2_e
  CPU_IR cpu_ir_1 (.i({undriven_3, cpu_accumulator_1_o_2}), .o(cpu_ir_1_o), .s(cpu_control_section_1_ir_s));
  // CPU_R cpu_r_4: pin names not known; wires that end beside it: cpu_accumulator_1_o_2, cpu_control_section_1_r3_s, cpu_accumulator_1_o_2, cpu_control_section_1_r3_e
  // CPU_RAM_256 cpu_ram_256_1: pin names not known; wires that end beside it: cpu_accumulator_1_o_2, cpu_control_section_1_mar_s, cpu_control_section_1_ram_e, cpu_control_section_1_ram_s, cpu_accumulator_1_o_2, cpu_accumulator_1_o_2, cpu_ram_256_1_p7
  // Pins of 8 and 16 bits meet at {cpu_accumulator_1_o, cpu_accumulator_1_o_2}
  // Pins of 8 and 16 bits meet at {undriven_2, cpu_accumulator_1_o_2}
  // Pins of 8 and 16 bits meet at {undriven_3, cpu_accumulator_1_o_2}
  // Pins of 8 and 16 bits meet at {undriven, cpu_accumulator_1_o_2}
endmodule
